// Logisim project multilevel_interrupt.circ as structural Verilog: 11 circuits, main circuit CPU
module CPU (
);

  wire alu_1_out_5, and_1_out, and_2_out, and_3_out, and_4_out, Beq, bgez, Bne, clk, cnt, d_ff_1_qn, eret,
       GO, Halt, Halt0, IE, IR, IR1, IR2, IR3, mfc0, mtc0, not_1_out, not_2_out, not_3_out, not_4_out,
       or_1_out, or_2_out, or_3_out, RF_SEL, RST, W1, W2, W3, \中断开关 , \控制器_1_dm_we , \控制器_1_imm_gates ,
       \控制器_1_jal , \控制器_1_lh , \控制器_1_memtoreg , \控制器_1_rf_we , \控制器_1_rw_sel , \控制器_1_shift , \控制器_1_slv ,
       \控制器_1_syscall , \控制器_1_x_sel , \控制器_1_y_sel ;
  wire [1:0] PC_sel, XY;
  wire [2:0] PBZ;
  wire [3:0] multiplexer_9_out, multiplexer_10_out, \控制器_1_alu_sel ;
  wire [4:0] decoder_1_r1_num, decoder_1_r2_num, decoder_1_rw;
  wire [5:0] decoder_1_func, decoder_1_op;
  wire [15:0] \decoder_1_立即数 , \总周期数 , \无条件分支指令数 , \有条件分支成功跳转 , \有条件分支指令数 ;
  wire [23:0] alu_1_result_2;
  wire [31:0] adder_1_out, alu_1_result, alu_in_1_x, alu_in_1_y, data_ext_1_dataout, demultiplexer_1_out0,
       EPC, \extender_1_立即数扩展 , mips_ram_1_p8, multiplexer_1_out, multiplexer_2_out, multiplexer_3_out,
       multiplexer_4_out, multiplexer_5_out, multiplexer_6_out, multiplexer_7_out, multiplexer_8_out,
       npc_1_npc, PC_q, reg_b, rf_1_reg_a, rom_1_data, SyscallOut, \屏蔽字输入 ;

  Button \u_总复位  (.out(RST));
  Button _1 (.out(IR1));
  Button _2 (.out(IR2));
  Button _3 (.out(IR3));
  LED led_1 (.in(W1));
  LED led_2 (.in(W2));
  LED led_3 (.in(W3));
  Hex_Digit_Display hex_digit_display_1 (.value(SyscallOut[31:28]));  // open: dp
  Demultiplexer #(.width(32), .enable("false")) demultiplexer_1 (
    .out0(demultiplexer_1_out0), .out1(\屏蔽字输入 ), .in(reg_b), .sel(RF_SEL));
  not not_1 (not_1_out, RF_SEL);
  and and_1 (and_1_out, mtc0, not_1_out);
  Multiplexer #(.width(32), .enable("false")) multiplexer_1 (
    .in0(npc_1_npc), .in1(demultiplexer_1_out0), .out(multiplexer_1_out), .sel(and_1_out));
  or or_1 (or_1_out, and_2_out, and_1_out);
  and and_2 (and_2_out, IR, IE);
  Hex_Digit_Display hex_digit_display_2 (.value(SyscallOut[27:24]));  // open: dp
  Hex_Digit_Display hex_digit_display_3 (.value(SyscallOut[23:20]));  // open: dp
  Register #(.width(32)) u_EPC (.D(multiplexer_1_out), .en(or_1_out), .Q(EPC), .clk(clk));  // open: clr
  Hex_Digit_Display hex_digit_display_4 (.value(SyscallOut[15:12]));  // open: dp
  Hex_Digit_Display hex_digit_display_5 (.value(SyscallOut[19:16]));  // open: dp
  and and_3 (and_3_out, IR, IE);
  Multiplexer #(.width(32), .enable("false")) multiplexer_2 (
    .in0(multiplexer_4_out), .in1(EPC), .out(multiplexer_2_out), .sel(eret));
  Hex_Digit_Display hex_digit_display_6 (.value(SyscallOut[7:4]));  // open: dp
  Hex_Digit_Display hex_digit_display_7 (.value(SyscallOut[11:8]));  // open: dp
  Multiplexer #(.select(2), .width(32), .enable("false")) multiplexer_3 (
    .in1(32'h3148), .in2(32'h325c), .in3(32'h336c), .out(multiplexer_3_out), .sel(XY));  // open: in0
  Multiplexer #(.width(32), .enable("false")) multiplexer_4 (
    .in0(npc_1_npc), .in1(multiplexer_3_out), .out(multiplexer_4_out), .sel(and_3_out));
  Hex_Digit_Display hex_digit_display_8 (.value(SyscallOut[3:0]));  // open: dp
  Clock u_clk (.out(clk));
  Register #(.width(32)) PC (.D(multiplexer_2_out), .en(not_2_out), .Q(PC_q), .clk(clk), .clr(RST));
  not not_2 (not_2_out, Halt);
  // Probe on \总周期数 
  // Probe on \无条件分支指令数 
  // Probe on \有条件分支成功跳转 
  ROM #(.addrWidth(10), .dataWidth(32)) rom_1 (
    .addr(PC_q[11:2]), .data({rom_1_data[31:12], RF_SEL, rom_1_data[10:0]}));  // open: sel
  Decoder decoder_1 (
    .PC({rom_1_data[31:12], RF_SEL, rom_1_data[10:0]}), .OP(decoder_1_op), .FUNC(decoder_1_func),
    .R1_num(decoder_1_r1_num), .R2_num(decoder_1_r2_num), .RW(decoder_1_rw), .\立即数 (\decoder_1_立即数 ),
    .syscall(\控制器_1_syscall ), .rW_sel(\控制器_1_rw_sel ), .jal(\控制器_1_jal ));
  Button u_GO (.out(GO));
  \控制器  \u_控制器_1  (
    .ALU_sel(\控制器_1_alu_sel ), .X_sel(\控制器_1_x_sel ), .syscall(\控制器_1_syscall ), .Y_sel(\控制器_1_y_sel ),
    .slv(\控制器_1_slv ), .bgez(bgez), .shift(\控制器_1_shift ), .jal(\控制器_1_jal ), .imm_gates(\控制器_1_imm_gates ),
    .beq(Beq), .DM_we(\控制器_1_dm_we ), .RF_WE(\控制器_1_rf_we ), .OP(decoder_1_op), .Funct(decoder_1_func),
    .rw_sel(\控制器_1_rw_sel ), .PC_sel(PC_sel), .bne(Bne), .lh(\控制器_1_lh ), .MemtoReg(\控制器_1_memtoreg ),
    .\input (rom_1_data[25:21]), .\中断开关 (\中断开关 ), .mtc0(mtc0), .mfc0(mfc0), .eret(eret));
  and and_4 (and_4_out, RF_SEL, mtc0);
  Multiplexer #(.width(32), .enable("false")) multiplexer_5 (
    .in0(multiplexer_7_out), .in1(multiplexer_6_out), .out(multiplexer_5_out), .sel(mfc0));
  Extender extender_1 (
    .\立即数 (\decoder_1_立即数 ), .\立即数扩展 (\extender_1_立即数扩展 ), .syscall(\控制器_1_syscall ),
    .imm_gates(\控制器_1_imm_gates ), .shift(\控制器_1_shift ));  // open: offset
  Multiplexer #(.width(32), .enable("false")) multiplexer_6 (
    .in0(EPC), .in1({{29{1'b0}}, PBZ}), .out(multiplexer_6_out), .sel(RF_SEL));
  RF rf_1 (
    .data(multiplexer_5_out), .clk(clk), .reg_a(rf_1_reg_a), .reg_b(reg_b), .we(\控制器_1_rf_we ),
    .rw(decoder_1_rw), .ra(decoder_1_r1_num), .rb(decoder_1_r2_num));
  Interrupt interrupt_1 (
    .\_1号中断 (IR1), .\_1号中断等待指示 (W1), .\_2号中断 (IR2), .\_2号中断等待指示 (W2), .\中断屏蔽字 (\屏蔽字输入 ), .\_3号中断 (IR3),
    .\_3号中断等待指示 (W3), .clk(clk), .\屏蔽字寄存器输出 (PBZ), .\中断屏蔽字寄存器使能端 (and_4_out), .eret(eret), .\中断开关 (\中断开关 ),
    .IE(IE), .IR(IR), .XY(XY));
  D_Flip_Flop d_ff_1 (.clk(clk), .D(Halt), .Qn(d_ff_1_qn), .reset(RST));  // open: Q, preset, en
  or or_2 (or_2_out, bgez, Beq, Bne);
  NPC npc_1 (
    .gez(not_3_out), .bgez(bgez), .beq_sign(Beq), .equal(alu_1_out_5), .bne_sign(Bne), .PC(PC_q),
    .A(rf_1_reg_a), .IR({rom_1_data[31:12], RF_SEL, rom_1_data[10:0]}), .offset(\extender_1_立即数扩展 ),
    .cnt(cnt), .nPC(npc_1_npc), .PC_sel(PC_sel));
  ALU_IN alu_in_1 (
    .A(rf_1_reg_a), .B(reg_b), .ext(\extender_1_立即数扩展 ), .X(alu_in_1_x), .Y(alu_in_1_y),
    .Y_sel(\控制器_1_y_sel ), .X_sel(\控制器_1_x_sel ), .bgez(bgez), .slv(\控制器_1_slv ));
  Counter #(.width(16), .max('hffff), .trigger("falling")) counter_1 (
    .count(d_ff_1_qn), .Q(\总周期数 ), .clk(clk), .clr(RST));  // open: load, D, carry
  Counter #(.width(16), .max('hffff), .trigger("falling")) counter_2 (
    .count(or_2_out), .Q(\有条件分支指令数 ), .clk(clk), .clr(RST));  // open: load, D, carry
  ALU alu_1 (
    .x(alu_in_1_x), .y(alu_in_1_y), .result({alu_1_result[31:26], alu_1_result_2, alu_1_result[1:0]}),
    .out_5(alu_1_out_5), .ALU_OP(\控制器_1_alu_sel ));
  Syscall syscall_1 (
    .reg_b(reg_b), .syscallout(SyscallOut), .halt(Halt0), .equal(alu_1_out_5), .syscall(\控制器_1_syscall ),
    .clk(clk), .RST(RST));
  Multiplexer #(.width(32), .enable("false")) multiplexer_7 (
    .in0(multiplexer_8_out), .in1(adder_1_out), .out(multiplexer_7_out), .sel(\控制器_1_jal ));
  not not_3 (not_3_out, alu_1_result[0]);
  Counter #(.width(16), .max('hffff), .trigger("falling")) counter_3 (
    .count(or_3_out), .Q(\无条件分支指令数 ), .clk(clk), .clr(RST));  // open: load, D, carry
  or or_3 (or_3_out, PC_sel[0], PC_sel[1]);
  Counter #(.width(16), .max('hffff), .trigger("falling")) counter_4 (
    .count(cnt), .Q(\有条件分支成功跳转 ), .clk(clk), .clr(RST));  // open: load, D, carry
  Multiplexer #(.width(32), .enable("false")) multiplexer_8 (
    .in0({alu_1_result[31:26], alu_1_result_2, alu_1_result[1:0]}), .in1(data_ext_1_dataout),
    .out(multiplexer_8_out), .sel(\控制器_1_memtoreg ));
  Multiplexer #(.width(4), .enable("false")) multiplexer_9 (
    .in0(4'b1111), .in1(multiplexer_10_out), .out(multiplexer_9_out), .sel(\控制器_1_lh ));
  Multiplexer #(.width(4), .enable("false")) multiplexer_10 (
    .in0(4'b0011), .in1(4'b1100), .out(multiplexer_10_out), .sel(alu_1_result[1]));
  // MIPS_RAM mips_ram_1: pin names not known; wires that end beside it: alu_1_result_2, reg_b, \控制器_1_dm_we , multiplexer_9_out, clk, \控制器_1_memtoreg , RST, mips_ram_1_p8
  Data_ext data_ext_1 (.datain(mips_ram_1_p8), .dataout(data_ext_1_dataout), .bit1(alu_1_result[1]), .lh(\控制器_1_lh ));
  Adder #(.width(32)) adder_1 (.a(PC_q), .b(32'h4), .out(adder_1_out));  // open: cin, cout
  Register #(.width(1)) register_1 (.D(Halt0), .en(not_4_out), .Q(Halt), .clk(clk), .clr(GO));
  not not_4 (not_4_out, Halt);

  // Notes on the sheet:
  //   中断源
  //   中断等待指示
  //   数码管输出应该用寄存器锁存，否则显示数据只能一闪而过
  //   可以通过项目增加Logisim库的方式将前几次实验完成的电路作为子电路引入到本电路中使用
  //   数码管输出
  //   总复位信号应将除ROM以外所有存储组件全部清零
  //   1546
  //   38
  //   338
  //   276
  //   指令存储器
  //   JR无须左移两位
  //   contents of rom_1 (hex, n*v repeats v):
  //   201d0200 20110200 20020022 112020 c 2231ffff 1620fffc 2002000a c 20150000 20160000 20170000 20080001
  //   20090003 20110876 118d00 112020 20020022 c 200b0008 1118806 1318806 112020 20020022 c 216bffff
  //   1560fff9 2002000a c 20150000 20160000 20170000 20080001 20090003 20110876 112020 20020022 c 200b0008
  //   1118804 1318804 112020 20020022 c 216bffff 1560fff9 2002000a c 20090000 200b0010 34118483 20120404
  //   118c00 129400 36318281 22520404 ad310000 2328820 21290004 216bffff 1560fffb 200b0020 20090000
  //   85310000 112020 20020022 c 21290002 216bffff 1560fff9 2002000a c 2011000f 112020 20020022 c 2231ffff
  //   621fffb 2002000a c 2002000a c afb00000 23bd0004 afb10000 23bd0004 afb20000 23bd0004 afb30000
  //   23bd0004 afb40000 23bd0004 afb50000 23bd0004 afb60000 23bd0004 afb70000 23bd0004 afa20000 23bd0004
  //   afa40000 23bd0004 40120000 afb20000 23bd0004 40120800 afb20004 23bd0004 20120001 40920800 d 20160001
  //   20140006 20150001 168020 108100 2149825 132020 20020022 c 1600fffa 295a022 1680fff7 d 23bdfffc
  //   8fb20000 40920800 23bdfffc 8fb20000 40920000 23bdfffc 8fa40000 23bdfffc 8fa20000 23bdfffc 8fb70000
  //   23bdfffc 8fb60000 23bdfffc 8fb50000 23bdfffc 8fb40000 23bdfffc 8fb30000 23bdfffc 8fb20000 23bdfffc
  //   8fb10000 23bdfffc 8fb00000 42000018 afb00000 23bd0004 afb10000 23bd0004 afb20000 23bd0004 afb30000
  //   23bd0004 afb40000 23bd0004 afb50000 23bd0004 afb60000 23bd0004 afb70000 23bd0004 afa20000 23bd0004
  //   afa40000 23bd0004 40120000 afb20000 40120800 afb20004 23bd0008 20120003 40920800 d 20160002 20140006
  //   20150001 168020 108100 2149825 132020 20020022 c 1600fffa 295a022 1680fff7 d 23bdfffc 8fb20000
  //   40920800 23bdfffc 8fb20000 40920000 23bdfffc 8fa40000 23bdfffc 8fa20000 23bdfffc 8fb70000 23bdfffc
  //   8fb60000 23bdfffc 8fb50000 23bdfffc 8fb40000 23bdfffc 8fb30000 23bdfffc 8fb20000 23bdfffc 8fb10000
  //   23bdfffc 8fb00000 42000018 afb00000 23bd0004 afb10000 23bd0004 afb20000 23bd0004 afb30000 23bd0004
  //   afb40000 23bd0004 afb50000 23bd0004 afb60000 23bd0004 afb70000 23bd0004 afa20000 23bd0004 afa40000
  //   23bd0004 40120000 afb20000 40120800 afb20004 23bd0008 20120007 40920800 d 20160003 20140006 20150001
  //   168020 108100 2149825 132020 20020022 c 1600ffb6 295a022 1680ffb3 d 23bdfffc 8fb20000 40920800
  //   23bdfffc 8fb20000 40920000 23bdfffc 8fa40000 23bdfffc 8fa20000 23bdfffc 8fb70000 23bdfffc 8fb60000
  //   23bdfffc 8fb50000 23bdfffc 8fb40000 23bdfffc 8fb30000 23bdfffc 8fb20000 23bdfffc 8fb10000 23bdfffc
  //   8fb00000 42000018
  //   存储单元均使用下降沿触发
  //   除了逻辑门立即数扩展为零扩展，其他均为符号扩展
  //   Continue with CCMB by one click for each instruction.
endmodule

// control
module \控制器  (
  input  [5:0] OP,
  input  [5:0] Funct,
  input  [4:0] \input ,
  output [3:0] ALU_sel,
  output X_sel,
  output syscall,
  output Y_sel,
  output slv,
  output bgez,
  output shift,
  output jal,
  output imm_gates,
  output beq,
  output DM_we,
  output RF_WE,
  output rw_sel,
  output [1:0] PC_sel,
  output bne,
  output lh,
  output MemtoReg,
  output \中断开关 ,
  output mtc0,
  output mfc0,
  output eret
);

  wire add, addi, addiu, addu, \and , andi, \break , comparator_1_eq, comparator_15_eq, comparator_16_eq,
       comparator_17_eq, comparator_18_eq, comparator_19_eq, comparator_20_eq, comparator_21_eq,
       comparator_22_eq, comparator_23_eq, comparator_24_eq, comparator_25_eq, comparator_26_eq,
       comparator_27_eq, comparator_28_eq, comparator_29_eq, comparator_30_eq, comparator_31_eq,
       comparator_32_eq, comparator_33_eq, comparator_34_eq, j, lw, \nor , \or , or_4_out, or_8_out,
       or_9_out, or_10_out, or_11_out, or_12_out, or_13_out, or_14_out, or_15_out, or_16_out, or_17_out,
       or_19_out, or_20_out, or_21_out, or_23_out, or_24_out, or_25_out, or_26_out, or_27_out, or_28_out,
       or_29_out, or_30_out, or_31_out, or_32_out, or_33_out, or_34_out, or_35_out, or_36_out, or_37_out,
       or_38_out, or_39_out, or_40_out, or_41_out, or_42_out, or_44_out, or_45_out, or_46_out, or_47_out,
       or_48_out, or_51_out, or_52_out, or_53_out, or_54_out, or_55_out, or_56_out, or_57_out, or_58_out,
       or_59_out, or_60_out, or_61_out, or_63_out, or_64_out, or_65_out, or_66_out, or_67_out, or_68_out,
       or_69_out, or_70_out, or_71_out, or_72_out, or_73_out, or_74_out, or_75_out, or_76_out, or_77_out,
       or_79_out, or_80_out, or_81_out, or_82_out, or_83_out, or_84_out, or_85_out, or_86_out, or_87_out,
       or_88_out, or_89_out, or_91_out, or_92_out, or_93_out, or_94_out, or_95_out, or_96_out, or_97_out,
       or_98_out, or_99_out, or_100_out, or_101_out, or_102_out, or_103_out, or_104_out, or_105_out, ori,
       sll, sllv, slt, slti, sltu, sra, srl, srlv, sub;

  Comparator #(.width(6)) comparator_1 (.a(OP), .b({6{1'b0}}), .eq(comparator_1_eq));  // open: gt, lt
  Comparator #(.width(6)) comparator_2 (.a(OP), .b(6'b001000), .eq(addi));  // open: gt, lt
  Comparator #(.width(6)) comparator_3 (.a(OP), .b(6'b001001), .eq(addiu));  // open: gt, lt
  Comparator #(.width(6)) comparator_4 (.a(OP), .b(6'b001100), .eq(andi));  // open: gt, lt
  Comparator #(.width(6)) comparator_5 (.a(OP), .b(6'b001101), .eq(ori));  // open: gt, lt
  Comparator #(.width(6)) comparator_6 (.a(OP), .b(6'b100011), .eq(lw));  // open: gt, lt
  Comparator #(.width(6)) comparator_7 (.a(OP), .b(6'b101011), .eq(DM_we));  // open: gt, lt
  Comparator #(.width(6)) comparator_8 (.a(OP), .b(6'b000100), .eq(beq));  // open: gt, lt
  Comparator #(.width(6)) comparator_9 (.a(OP), .b(6'b000101), .eq(bne));  // open: gt, lt
  Comparator #(.width(6)) comparator_10 (.a(OP), .b(6'b001010), .eq(slti));  // open: gt, lt
  Comparator #(.width(6)) comparator_11 (.a(OP), .b(6'b000010), .eq(j));  // open: gt, lt
  Comparator #(.width(6)) comparator_12 (.a(OP), .b(6'b000011), .eq(jal));  // open: gt, lt
  Comparator #(.width(6)) comparator_13 (.a(OP), .b(6'b100001), .eq(lh));  // open: gt, lt
  Comparator #(.width(6)) comparator_14 (.a(OP), .b(6'b000001), .eq(bgez));  // open: gt, lt
  Comparator #(.width(6)) comparator_15 (.a(OP), .b(6'b010000), .eq(comparator_15_eq));  // open: gt, lt
  Comparator #(.width(6)) comparator_16 (.a(Funct), .b(6'b100000), .eq(comparator_16_eq));  // open: gt, lt
  Comparator #(.width(6)) comparator_17 (.a(Funct), .b(6'b100001), .eq(comparator_17_eq));  // open: gt, lt
  Comparator #(.width(6)) comparator_18 (.a(Funct), .b(6'b100100), .eq(comparator_18_eq));  // open: gt, lt
  Comparator #(.width(6)) comparator_19 (.a(Funct), .b({6{1'b0}}), .eq(comparator_19_eq));  // open: gt, lt
  Comparator #(.width(6)) comparator_20 (.a(Funct), .b(6'b000011), .eq(comparator_20_eq));  // open: gt, lt
  Comparator #(.width(6)) comparator_21 (.a(Funct), .b(6'b000010), .eq(comparator_21_eq));  // open: gt, lt
  Comparator #(.width(6)) comparator_22 (.a(Funct), .b(6'b100010), .eq(comparator_22_eq));  // open: gt, lt
  Comparator #(.width(6)) comparator_23 (.a(Funct), .b(6'b100101), .eq(comparator_23_eq));  // open: gt, lt
  Comparator #(.width(6)) comparator_24 (.a(Funct), .b(6'b100111), .eq(comparator_24_eq));  // open: gt, lt
  Comparator #(.width(6)) comparator_25 (.a(Funct), .b(6'b101010), .eq(comparator_25_eq));  // open: gt, lt
  Comparator #(.width(6)) comparator_26 (.a(Funct), .b(6'b101011), .eq(comparator_26_eq));  // open: gt, lt
  Comparator #(.width(6)) comparator_27 (.a(Funct), .b(6'b001000), .eq(comparator_27_eq));  // open: gt, lt
  Comparator #(.width(6)) comparator_28 (.a(Funct), .b(6'b000110), .eq(comparator_28_eq));  // open: gt, lt
  Comparator #(.width(6)) comparator_29 (.a(Funct), .b(6'b000100), .eq(comparator_29_eq));  // open: gt, lt
  Comparator #(.width(6)) comparator_30 (.a(Funct), .b(6'b001100), .eq(comparator_30_eq));  // open: gt, lt
  Comparator #(.width(6)) comparator_31 (.a(Funct), .b(6'b001101), .eq(comparator_31_eq));  // open: gt, lt
  Comparator #(.width(6)) comparator_32 (.a(Funct), .b(6'b011000), .eq(comparator_32_eq));  // open: gt, lt
  Comparator #(.width(5)) comparator_33 (.a(\input ), .b({5{1'b0}}), .eq(comparator_33_eq));  // open: gt, lt
  Comparator #(.width(5)) comparator_34 (.a(\input ), .b(5'b00100), .eq(comparator_34_eq));  // open: gt, lt
  and and_1 (add, comparator_1_eq, comparator_16_eq);
  and and_2 (addu, comparator_1_eq, comparator_17_eq);
  and and_3 (\and , comparator_1_eq, comparator_18_eq);
  and and_4 (sll, comparator_1_eq, comparator_19_eq);
  and and_5 (sra, comparator_1_eq, comparator_20_eq);
  and and_6 (srl, comparator_1_eq, comparator_21_eq);
  and and_7 (sub, comparator_1_eq, comparator_22_eq);
  and and_8 (\or , comparator_1_eq, comparator_23_eq);
  and and_9 (\nor , comparator_1_eq, comparator_24_eq);
  and and_10 (slt, comparator_1_eq, comparator_25_eq);
  and and_11 (sltu, comparator_1_eq, comparator_26_eq);
  and and_12 (PC_sel[1], comparator_1_eq, comparator_27_eq);
  and and_13 (srlv, comparator_1_eq, comparator_28_eq);
  and and_14 (sllv, comparator_1_eq, comparator_29_eq);
  and and_15 (syscall, comparator_1_eq, comparator_30_eq);
  and and_16 (\break , comparator_1_eq, comparator_31_eq);
  and and_17 (eret, comparator_15_eq, comparator_32_eq);
  and and_18 (mfc0, comparator_15_eq, comparator_33_eq);
  and and_19 (mtc0, comparator_15_eq, comparator_34_eq);
  or or_1 (slv, sllv, srlv);
  or or_2 (\中断开关 , \break , eret);
  or or_3 (shift, sll, or_4_out);
  or or_4 (or_4_out, srl, sra);
  or or_5 (imm_gates, andi, ori);
  or or_6 (MemtoReg, lw, lh);
  or or_7 (Y_sel, addi, or_8_out);
  or or_8 (or_8_out, or_9_out, andi);
  or or_9 (or_9_out, addiu, or_10_out);
  or or_10 (or_10_out, or_11_out, sra);
  or or_11 (or_11_out, or_12_out, slti);
  or or_12 (or_12_out, srl, or_13_out);
  or or_13 (or_13_out, or_14_out, sll);
  or or_14 (or_14_out, ori, or_15_out);
  or or_15 (or_15_out, or_16_out, DM_we);
  or or_16 (or_16_out, syscall, or_17_out);
  or or_17 (or_17_out, lw, lh);
  or or_18 (X_sel, sra, or_19_out);
  or or_19 (or_19_out, srl, or_20_out);
  or or_20 (or_20_out, sll, or_21_out);
  or or_21 (or_21_out, sllv, srlv);
  or or_22 (RF_WE, addu, or_23_out);
  or or_23 (or_23_out, or_24_out, addiu);
  or or_24 (or_24_out, andi, or_25_out);
  or or_25 (or_25_out, or_26_out, addi);
  or or_26 (or_26_out, sllv, or_27_out);
  or or_27 (or_27_out, or_28_out, srlv);
  or or_28 (or_28_out, slti, or_29_out);
  or or_29 (or_29_out, or_30_out, sltu);
  or or_30 (or_30_out, add, or_31_out);
  or or_31 (or_31_out, or_32_out, sub);
  or or_32 (or_32_out, \and , or_33_out);
  or or_33 (or_33_out, or_34_out, sra);
  or or_34 (or_34_out, \nor , or_35_out);
  or or_35 (or_35_out, or_36_out, slt);
  or or_36 (or_36_out, ori, or_37_out);
  or or_37 (or_37_out, or_38_out, srl);
  or or_38 (or_38_out, sll, or_39_out);
  or or_39 (or_39_out, or_40_out, jal);
  or or_40 (or_40_out, or_41_out, lh);
  or or_41 (or_41_out, \or , or_42_out);
  or or_42 (or_42_out, mfc0, lw);
  or or_43 (rw_sel, addi, or_44_out);
  or or_44 (or_44_out, or_45_out, addiu);
  or or_45 (or_45_out, or_46_out, slti);
  or or_46 (or_46_out, or_47_out, lw);
  or or_47 (or_47_out, ori, or_48_out);
  or or_48 (or_48_out, lh, mfc0);
  or or_49 (PC_sel[0], j, jal);
  or or_50 (ALU_sel[3], \nor , or_51_out);
  or or_51 (or_51_out, \or , or_52_out);
  or or_52 (or_52_out, ori, or_53_out);
  or or_53 (or_53_out, or_54_out, bne);
  or or_54 (or_54_out, beq, or_55_out);
  or or_55 (or_55_out, or_56_out, sltu);
  or or_56 (or_56_out, slti, or_57_out);
  or or_57 (or_57_out, or_58_out, slt);
  or or_58 (or_58_out, jal, or_59_out);
  or or_59 (or_59_out, or_60_out, syscall);
  or or_60 (or_60_out, j, or_61_out);
  or or_61 (or_61_out, bgez, PC_sel[1]);
  or or_62 (ALU_sel[2], addi, or_63_out);
  or or_63 (or_63_out, or_64_out, addiu);
  or or_64 (or_64_out, addu, or_65_out);
  or or_65 (or_65_out, or_66_out, syscall);
  or or_66 (or_66_out, andi, or_67_out);
  or or_67 (or_67_out, or_68_out, sub);
  or or_68 (or_68_out, sltu, or_69_out);
  or or_69 (or_69_out, or_70_out, \and );
  or or_70 (or_70_out, bne, or_71_out);
  or or_71 (or_71_out, or_72_out, beq);
  or or_72 (or_72_out, add, or_73_out);
  or or_73 (or_73_out, or_74_out, jal);
  or or_74 (or_74_out, PC_sel[1], or_75_out);
  or or_75 (or_75_out, or_76_out, DM_we);
  or or_76 (or_76_out, lw, or_77_out);
  or or_77 (or_77_out, j, lh);
  or or_78 (ALU_sel[1], \and , or_79_out);
  or or_79 (or_79_out, or_80_out, andi);
  or or_80 (or_80_out, srl, or_81_out);
  or or_81 (or_81_out, or_82_out, sub);
  or or_82 (or_82_out, \nor , or_83_out);
  or or_83 (or_83_out, or_84_out, slti);
  or or_84 (or_84_out, srlv, or_85_out);
  or or_85 (or_85_out, or_86_out, slt);
  or or_86 (or_86_out, jal, or_87_out);
  or or_87 (or_87_out, or_88_out, syscall);
  or or_88 (or_88_out, PC_sel[1], or_89_out);
  or or_89 (or_89_out, j, bgez);
  or or_90 (ALU_sel[0], addu, or_91_out);
  or or_91 (or_91_out, or_92_out, addiu);
  or or_92 (or_92_out, andi, or_93_out);
  or or_93 (or_93_out, or_94_out, add);
  or or_94 (or_94_out, addi, or_95_out);
  or or_95 (or_95_out, or_96_out, \and );
  or or_96 (or_96_out, sra, or_97_out);
  or or_97 (or_97_out, or_98_out, slti);
  or or_98 (or_98_out, slt, or_99_out);
  or or_99 (or_99_out, or_100_out, syscall);
  or or_100 (or_100_out, or_101_out, jal);
  or or_101 (or_101_out, lh, or_102_out);
  or or_102 (or_102_out, j, or_103_out);
  or or_103 (or_103_out, or_104_out, DM_we);
  or or_104 (or_104_out, PC_sel[1], or_105_out);
  or or_105 (or_105_out, bgez, lw);

  // Other names for the same wires on the sheet: jr = PC_sel[1]; sw = DM_we
endmodule

// Ext
module Extender (
  input  syscall,
  input  [15:0] \立即数 ,
  input  imm_gates,
  input  shift,
  output [31:0] \立即数扩展 ,
  output [31:0] offset
);

  wire [15:0] multiplexer_1_out;
  wire [31:0] bit_extender_1_out, bit_extender_2_out, bit_extender_3_out, multiplexer_2_out;

  Multiplexer #(.width(16), .enable("false")) multiplexer_1 (
    .in0(\立即数 ), .in1(16'ha), .out(multiplexer_1_out), .sel(syscall));
  assign bit_extender_1_out = {{16{multiplexer_1_out[15]}}, multiplexer_1_out};  // Bit_Extender bit_extender_1
  assign bit_extender_2_out = {{16{1'b0}}, multiplexer_1_out};  // Bit_Extender bit_extender_2
  assign bit_extender_3_out = {{27{\立即数 [10]}}, \立即数 [10:6]};  // Bit_Extender bit_extender_3
  assign offset = {{16{\立即数 [15]}}, \立即数 };  // Bit_Extender bit_extender_4
  Multiplexer #(.width(32), .enable("false")) multiplexer_2 (
    .in0(bit_extender_1_out), .in1(bit_extender_2_out), .out(multiplexer_2_out), .sel(imm_gates));
  Multiplexer #(.width(32), .enable("false")) multiplexer_3 (
    .in0(multiplexer_2_out), .in1(bit_extender_3_out), .out(\立即数扩展 ), .sel(shift));
endmodule

module Decoder (
  input  syscall,
  input  [31:0] PC,
  input  rW_sel,
  input  jal,
  output [5:0] OP,
  output [5:0] FUNC,
  output [4:0] R1_num,
  output [4:0] R2_num,
  output [4:0] RW,
  output [15:0] \立即数 
);

  wire [4:0] multiplexer_3_out;

  Multiplexer #(.width(5), .enable("false")) multiplexer_1 (
    .in0(PC[25:21]), .in1(5'b00010), .out(R1_num), .sel(syscall));
  Multiplexer #(.width(5), .enable("false")) multiplexer_2 (
    .in0(PC[20:16]), .in1(5'b00100), .out(R2_num), .sel(syscall));
  Multiplexer #(.width(5), .enable("false")) multiplexer_3 (
    .in0(PC[15:11]), .in1(PC[20:16]), .out(multiplexer_3_out), .sel(rW_sel));
  Multiplexer #(.width(5), .enable("false")) multiplexer_4 (
    .in0(multiplexer_3_out), .in1({5{1'b1}}), .out(RW), .sel(jal));

  assign FUNC = PC[5:0];
  assign OP = PC[31:26];
  assign \立即数  = PC[15:0];
endmodule

module NPC (
  input  gez,
  input  bgez,
  input  beq_sign,
  input  equal,
  input  bne_sign,
  input  [1:0] PC_sel,
  input  [31:0] PC,
  input  [31:0] A,
  input  [31:0] IR,
  input  [31:0] offset,
  output cnt,
  output [31:0] nPC
);

  wire and_1_out, and_2_out, and_3_out, not_1_out;
  wire [31:0] adder_1_out, adder_2_out, multiplexer_1_out, shifter_1_out;

  Adder #(.width(32)) adder_1 (.a(PC), .b(32'h4), .out(adder_1_out));  // open: cin, cout
  Shifter #(.width(32)) shifter_1 (.in(offset), .\dist (5'b00010), .out(shifter_1_out));
  not not_1 (not_1_out, equal);
  Adder #(.width(32)) adder_2 (.a(adder_1_out), .b(shifter_1_out), .out(adder_2_out));  // open: cin, cout
  and and_1 (and_1_out, gez, bgez);
  and and_2 (and_2_out, beq_sign, equal);
  and and_3 (and_3_out, not_1_out, bne_sign);
  or or_1 (cnt, and_1_out, and_2_out, and_3_out);
  Multiplexer #(.select(2), .width(32), .enable("false")) multiplexer_1 (
    .in0(adder_1_out), .in1({4'b0000, IR[25:0], 2'b00}), .in2(A), .in3({32{1'b0}}), .out(multiplexer_1_out),
    .sel(PC_sel));
  Multiplexer #(.width(32), .enable("false")) multiplexer_2 (
    .in0(multiplexer_1_out), .in1(adder_2_out), .out(nPC), .sel(cnt));
endmodule

module ALU (
  input  [31:0] x,
  input  [31:0] y,
  input  [3:0] ALU_OP,
  output [31:0] result,
  output out_5
);

  ALU_part alu_1 (
    .AluOP(ALU_OP), .X(x), .Equal(out_5), .Result(result), .Y(y));  // open: Signed_Overflow, Result_2, UnSigned_Overflow
endmodule

module RF (
  input  [31:0] data,
  input  clk,
  input  we,
  input  [4:0] rw,
  input  [4:0] rb,
  input  [4:0] ra,
  output [31:0] reg_a,
  output [31:0] reg_b
);

  // RegisterFile registerfile_1: pin names not known; wires that end beside it: data, clk, we, rw, ra, rb, reg_a, reg_b
endmodule

// ALU_in
module ALU_IN (
  input  Y_sel,
  input  X_sel,
  input  bgez,
  input  slv,
  input  [31:0] A,
  input  [31:0] B,
  input  [31:0] ext,
  output [31:0] X,
  output [31:0] Y
);

  wire [31:0] multiplexer_1_out, multiplexer_3_out;

  Multiplexer #(.width(32), .enable("false")) multiplexer_1 (.in0(B), .in1(ext), .out(multiplexer_1_out), .sel(Y_sel));
  Multiplexer #(.width(32), .enable("false")) multiplexer_2 (.in0(A), .in1(B), .out(X), .sel(X_sel));
  Multiplexer #(.width(32), .enable("false")) multiplexer_3 (
    .in0(multiplexer_1_out), .in1({32{1'b0}}), .out(multiplexer_3_out), .sel(bgez));
  Multiplexer #(.width(32), .enable("false")) multiplexer_4 (.in0(multiplexer_3_out), .in1(A), .out(Y), .sel(slv));
endmodule

// syscall
module Syscall (
  input  equal,
  input  syscall,
  input  [31:0] reg_b,
  input  clk,
  input  RST,
  output [31:0] syscallout,
  output halt
);

  wire and_2_out, not_1_out;

  not not_1 (not_1_out, equal);
  and and_1 (halt, equal, syscall);
  and and_2 (and_2_out, syscall, not_1_out);
  Register #(.width(32)) register_1 (.D(reg_b), .en(and_2_out), .Q(syscallout), .clk(clk), .clr(RST));
endmodule

module Data_ext (
  input  [31:0] datain,
  input  lh,
  input  bit1,
  output [31:0] dataout
);

  wire [31:0] bit_extender_1_out, bit_extender_2_out, multiplexer_1_out;

  assign bit_extender_1_out = {{16{datain[15]}}, datain[15:0]};  // Bit_Extender bit_extender_1
  assign bit_extender_2_out = {{16{datain[31]}}, datain[31:16]};  // Bit_Extender bit_extender_2
  Multiplexer #(.width(32), .enable("false")) multiplexer_1 (
    .in0(bit_extender_1_out), .in1(bit_extender_2_out), .out(multiplexer_1_out), .sel(bit1));
  Multiplexer #(.width(32), .enable("false")) multiplexer_2 (
    .in0(datain), .in1(multiplexer_1_out), .out(dataout), .sel(lh));
endmodule

module Interrupt (
  input  \_1号中断 ,
  input  \_2号中断 ,
  input  [31:0] \中断屏蔽字 ,
  input  \中断屏蔽字寄存器使能端 ,
  input  \_3号中断 ,
  input  clk,
  input  \中断开关 ,
  input  eret,
  output \_1号中断等待指示 ,
  output [1:0] XY,
  output \_2号中断等待指示 ,
  output IR,
  output [2:0] \屏蔽字寄存器输出 ,
  output \_3号中断等待指示 ,
  output IE
);

  wire \_1号清零 , \_2号清零 , \_3号清零 , and_1_out, and_2_out, and_3_out, and_4_out, and_5_out, and_6_out,
       and_7_out, d_ff_1_q, d_ff_2_q, d_ff_3_q, IR1_2_q, IR1_3_q, IR1_q, not_1_out, not_2_out, not_3_out,
       or_4_out, or_5_out, or_6_out, or_7_out;
  wire [1:0] multiplexer_1_out, multiplexer_2_out;

  D_Flip_Flop d_ff_1 (.clk(\_1号中断 ), .D(1'b1), .Q(d_ff_1_q), .reset(IR1_q));  // open: Qn, preset, en
  or or_1 (\_1号中断等待指示 , IR1_q, d_ff_1_q);
  D_Flip_Flop d_ff_2 (.clk(\_2号中断 ), .D(1'b1), .Q(d_ff_2_q), .reset(IR1_2_q));  // open: Qn, preset, en
  or or_2 (\_2号中断等待指示 , IR1_2_q, d_ff_2_q);
  D_Flip_Flop d_ff_3 (.clk(\_3号中断 ), .D(1'b1), .Q(d_ff_3_q), .reset(IR1_3_q));  // open: Qn, preset, en
  or or_3 (\_3号中断等待指示 , IR1_3_q, d_ff_3_q);
  LED _1 (.in(\_1号中断等待指示 ));
  LED _2 (.in(\_2号中断等待指示 ));
  LED _3 (.in(\_3号中断等待指示 ));
  or or_4 (or_4_out, d_ff_1_q, IR1_q);
  and and_1 (and_1_out, or_4_out, ~\_1号清零 );  // AND_Gate
  or or_5 (or_5_out, d_ff_2_q, IR1_2_q);
  and and_2 (and_2_out, or_5_out, ~\_2号清零 );  // AND_Gate
  or or_6 (or_6_out, d_ff_3_q, IR1_3_q);
  and and_3 (and_3_out, or_6_out, ~\_3号清零 );  // AND_Gate
  D_Flip_Flop IR1 (.clk(clk), .D(and_1_out), .Q(IR1_q));  // open: Qn, preset, en, reset
  D_Flip_Flop IR1_2 (.clk(clk), .D(and_2_out), .Q(IR1_2_q));  // open: Qn, preset, en, reset
  D_Flip_Flop IR1_3 (.clk(clk), .D(and_3_out), .Q(IR1_3_q));  // open: Qn, preset, en, reset
  Register #(.width(3)) register_1 (.D(\中断屏蔽字 [2:0]), .en(\中断屏蔽字寄存器使能端 ), .Q(\屏蔽字寄存器输出 ), .clk(clk));  // open: clr
  not not_1 (not_1_out, \屏蔽字寄存器输出 [0]);
  not not_2 (not_2_out, \屏蔽字寄存器输出 [1]);
  not not_3 (not_3_out, \屏蔽字寄存器输出 [2]);
  and and_4 (and_4_out, \_1号中断等待指示 , not_1_out);
  and and_5 (and_5_out, \_2号中断等待指示 , not_2_out);
  and and_6 (and_6_out, \_3号中断等待指示 , not_3_out);
  D_Flip_Flop d_ff_4 (.clk(clk), .D(IE), .Qn(IE), .en(or_7_out));  // open: Q, preset, reset
  or or_7 (or_7_out, and_7_out, eret, \中断开关 );
  and and_7 (and_7_out, IR, IE);
  or or_8 (IR, and_6_out, and_5_out, and_4_out);
  Multiplexer #(.width(2), .enable("false")) multiplexer_1 (
    .in0(2'b00), .in1(2'b01), .out(multiplexer_1_out), .sel(\_1号中断等待指示 ));
  Multiplexer #(.width(2), .enable("false")) multiplexer_2 (
    .in0(multiplexer_1_out), .in1(2'b10), .out(multiplexer_2_out), .sel(\_2号中断等待指示 ));
  Multiplexer #(.width(2), .enable("false")) multiplexer_3 (
    .in0(multiplexer_2_out), .in1(2'b11), .out(XY), .sel(\_3号中断等待指示 ));
  Demultiplexer #(.select(2), .enable("false")) demultiplexer_1 (
    .out1(\_1号清零 ), .out2(\_2号清零 ), .out3(\_3号清零 ), .in(eret), .sel(XY));  // open: out0

  // Other names for the same wires on the sheet: 中断 = IR

  // Notes on the sheet:
  //   中断信号源及指示电路规范（优先级3>2>1>CPU(0）)
  //   中断信号采样参考电路
  //   中断信号采样参考电路
  //   中断信号采样参考电路
  //   Reset 
  //   Reset 
  //   Reset 
endmodule
