// Logisim project interrupt_of_pipelineCPU.circ as structural Verilog: 17 circuits, main circuit CPU
module CPU (
);

  wire alu_1_out_5, and_1_out, and_2_out, and_3_out, b, Beq, bgez, Bne, CBScnt, clk, comparator_1_eq,
       comparator_2_eq, d_ff_1_qn, eret, ex_mem_1_dm_we_2, ex_mem_1_halt_3, ex_mem_1_jal_2, ex_mem_1_lh_2,
       ex_mem_1_memtoreg_2, ex_mem_1_rf_we_2, GO, Halt, Halt0, hazzard_unit_1_bubid, hazzard_unit_1_bubif,
       hazzard_unit_1_stall, id_ex_1_dm_we_2, id_ex_1_jal_2, id_ex_1_lh_2, id_ex_1_slv_2, id_ex_1_syscall_2,
       id_ex_1_x_sel_2, id_ex_1_y_sel_2, IE, IR, IR1, IR2, IR3, jump, mem_wb_1_jal_2, mem_wb_1_memtoreg_2,
       mem_wb_1_rf_we_2, MemtoReg, not_1_out, not_2_out, not_3_out, or_1_out, or_3_out, or_4_out, RST,
       syscall_1_halt, W1, W2, W3, WE_EX, \控制器_1_beq , \控制器_1_bgez , \控制器_1_bne , \控制器_1_dm_we ,
       \控制器_1_eret , \控制器_1_imm_gates , \控制器_1_jal , \控制器_1_lh , \控制器_1_memtoreg , \控制器_1_rf_we ,
       \控制器_1_rw_sel , \控制器_1_shift , \控制器_1_slv , \控制器_1_syscall , \控制器_1_x_sel , \控制器_1_y_sel ;
  wire [1:0] PC_sel, XY, \控制器_1_pc_sel ;
  wire [3:0] id_ex_1_alu_sel_2, multiplexer_9_out, multiplexer_10_out, sel, \控制器_1_alu_sel ;
  wire [4:0] decoder_1_r1_num, decoder_1_r2_num, decoder_1_rw, ex_mem_1_rw_2, id_ex_1_rw_2, mem_wb_1_rw_2,
       RA_EX, RB_EX;
  wire [5:0] decoder_1_func, decoder_1_op;
  wire [15:0] \decoder_1_立即数 , \load_use次数 , \总周期数 , \无条件分支指令数 , \有条件分支成功跳转 , \有条件分支指令数 ;
  wire [31:0] adder_1_out, adder_2_out, alu_1_result, alu_in_1_reg_a, alu_in_1_reg_b, alu_in_1_x, alu_in_1_y,
       data_ext_1_dataout, EPC, ex_mem_1_pc_out, ex_mem_1_reg_b_2, ex_mem_1_result_2, \extender_1_立即数扩展 ,
       id_ex_1_ext_2, id_ex_1_ir_out, id_ex_1_reg_a_2, id_ex_1_reg_b_2, if_id_1_ir_out, mem_wb_1_dm_out_2,
       mem_wb_1_pc_out, mem_wb_1_result_2, mips_ram_1_p7, multiplexer_1_out, multiplexer_2_out,
       multiplexer_3_out, multiplexer_4_out, multiplexer_5_out, multiplexer_6_out, multiplexer_8_out,
       npc_1_npc, PC_EX, PC_ID, PC_q, result, rf_1_reg_a, rf_1_reg_b, RF_data, rom_1_data, SyscallOut;

  Button \u_总复位  (.out(RST));
  Button _1 (.out(IR1));
  Button _2 (.out(IR2));
  Button _3 (.out(IR3));
  Clock u_clk (.out(clk));
  LED led_1 (.in(W1));
  LED led_2 (.in(W2));
  LED led_3 (.in(W3));
  Multiplexer #(.width(32), .enable("false")) multiplexer_1 (
    .in0(PC_ID), .in1(npc_1_npc), .out(multiplexer_1_out), .sel(jump));
  Multiplexer #(.width(32), .enable("false")) multiplexer_2 (
    .in0(multiplexer_1_out), .in1(PC_q), .out(multiplexer_2_out), .sel(b));
  Register #(.width(32)) u_EPC (.D(multiplexer_2_out), .en(and_1_out), .Q(EPC), .clk(clk));  // open: clr
  and and_1 (and_1_out, IR, IE);
  not not_1 (not_1_out, Halt);
  Hex_Digit_Display hex_digit_display_1 (.value(SyscallOut[31:28]));  // open: dp
  Multiplexer #(.width(32), .enable("false")) multiplexer_3 (
    .in0(multiplexer_5_out), .in1(EPC), .out(multiplexer_3_out), .sel(eret));
  Hex_Digit_Display hex_digit_display_2 (.value(SyscallOut[23:20]));  // open: dp
  Hex_Digit_Display hex_digit_display_3 (.value(SyscallOut[27:24]));  // open: dp
  and and_2 (and_2_out, IR, IE);
  Hex_Digit_Display hex_digit_display_4 (.value(SyscallOut[15:12]));  // open: dp
  Hex_Digit_Display hex_digit_display_5 (.value(SyscallOut[19:16]));  // open: dp
  Multiplexer #(.select(2), .width(32), .enable("false")) multiplexer_4 (
    .in1(32'h3148), .in2(32'h321c), .in3(32'h32f0), .out(multiplexer_4_out), .sel(XY));  // open: in0
  Multiplexer #(.width(32), .enable("false")) multiplexer_5 (
    .in0(multiplexer_6_out), .in1(multiplexer_4_out), .out(multiplexer_5_out), .sel(and_2_out));
  interrupt interrupt_1 (
    .\_1号中断 (IR1), .\_1号中断等待指示 (W1), .\_2号中断 (IR2), .\_2号中断等待指示 (W2), .\_3号中断 (IR3), .\_3号中断等待指示 (W3),
    .clk(clk), .eret(eret), .XY(XY), .IE(IE), .IR(IR));
  Hex_Digit_Display hex_digit_display_6 (.value(SyscallOut[7:4]));  // open: dp
  Hex_Digit_Display hex_digit_display_7 (.value(SyscallOut[11:8]));  // open: dp
  Hex_Digit_Display hex_digit_display_8 (.value(SyscallOut[3:0]));  // open: dp
  Register #(.width(32)) PC (.D(multiplexer_3_out), .en(hazzard_unit_1_stall), .Q(PC_q), .clk(clk), .clr(RST));
  // Probe on \总周期数 
  // Probe on \无条件分支指令数 
  // Probe on \有条件分支成功跳转 
  // Probe on \load_use次数 
  Multiplexer #(.width(32), .enable("false")) multiplexer_6 (
    .in0(adder_1_out), .in1(npc_1_npc), .out(multiplexer_6_out), .sel(jump));
  Adder #(.width(32)) adder_1 (.a(PC_q), .b(32'h4), .out(adder_1_out));  // open: cin, cout
  ROM #(.addrWidth(10), .dataWidth(32)) rom_1 (.addr(PC_q[11:2]), .data(rom_1_data));  // open: sel
  IF_ID if_id_1 (
    .PC_in(PC_q), .ir_in(rom_1_data), .PC_out(PC_ID), .ir_out(if_id_1_ir_out), .Halt(hazzard_unit_1_stall),
    .clk(clk), .clear(RST), .BUBIF(hazzard_unit_1_bubif));
  Button u_GO (.out(GO));
  Decoder decoder_1 (
    .PC(if_id_1_ir_out), .OP(decoder_1_op), .FUNC(decoder_1_func), .R1_num(decoder_1_r1_num),
    .R2_num(decoder_1_r2_num), .RW(decoder_1_rw), .\立即数 (\decoder_1_立即数 ), .syscall(\控制器_1_syscall ),
    .rW_sel(\控制器_1_rw_sel ), .jal(\控制器_1_jal ));
  Hazzard_Unit hazzard_unit_1 (
    .RAID(decoder_1_r1_num), .WE_EX(WE_EX), .RWEX(id_ex_1_rw_2), .RBID(decoder_1_r2_num), .Jump(jump),
    .rst(RST), .clk(clk), .Stall(hazzard_unit_1_stall), .BUBID(hazzard_unit_1_bubid),
    .BUBIF(hazzard_unit_1_bubif), .nHalt(not_1_out), .\气泡数 (\load_use次数 ), .MemtoReg(MemtoReg), .RAEX(RA_EX),
    .sel(sel), .RWWB(mem_wb_1_rw_2), .RBEX(RB_EX), .WE_WB(mem_wb_1_rf_we_2), .WE_MEM(ex_mem_1_rf_we_2),
    .RWMEM(ex_mem_1_rw_2), .irie(and_3_out), .eret(eret));
  \控制器  \u_控制器_1  (
    .ALU_sel(\控制器_1_alu_sel ), .X_sel(\控制器_1_x_sel ), .syscall(\控制器_1_syscall ), .Y_sel(\控制器_1_y_sel ),
    .slv(\控制器_1_slv ), .bgez(\控制器_1_bgez ), .shift(\控制器_1_shift ), .jal(\控制器_1_jal ),
    .imm_gates(\控制器_1_imm_gates ), .beq(\控制器_1_beq ), .DM_we(\控制器_1_dm_we ), .RF_WE(\控制器_1_rf_we ),
    .OP(decoder_1_op), .Funct(decoder_1_func), .rw_sel(\控制器_1_rw_sel ), .PC_sel(\控制器_1_pc_sel ),
    .bne(\控制器_1_bne ), .lh(\控制器_1_lh ), .MemtoReg(\控制器_1_memtoreg ), .eret(\控制器_1_eret ));
  or or_1 (or_1_out, PC_sel[0], PC_sel[1]);
  Extender extender_1 (
    .\立即数 (\decoder_1_立即数 ), .\立即数扩展 (\extender_1_立即数扩展 ), .syscall(\控制器_1_syscall ),
    .imm_gates(\控制器_1_imm_gates ), .shift(\控制器_1_shift ));  // open: offset
  and and_3 (and_3_out, IR, IE);
  or or_2 (jump, or_1_out, CBScnt);
  RF rf_1 (
    .data(RF_data), .clk(clk), .reg_a(rf_1_reg_a), .reg_b(rf_1_reg_b), .we(mem_wb_1_rf_we_2),
    .rw(mem_wb_1_rw_2), .ra(decoder_1_r1_num), .rb(decoder_1_r2_num));
  ID_EX id_ex_1 (
    .PC_in(PC_ID), .Halt(not_1_out), .clk(clk), .RF_we(\控制器_1_rf_we ), .MemtoReg(\控制器_1_memtoreg ),
    .jal(\控制器_1_jal ), .DM_we(\控制器_1_dm_we ), .lh(\控制器_1_lh ), .bne(\控制器_1_bne ), .beq(\控制器_1_beq ),
    .bgez(\控制器_1_bgez ), .PC_sel(\控制器_1_pc_sel ), .slv(\控制器_1_slv ), .syscall(\控制器_1_syscall ),
    .ALU_sel(\控制器_1_alu_sel ), .Y_sel(\控制器_1_y_sel ), .X_sel(\控制器_1_x_sel ), .Reg_a(rf_1_reg_a),
    .Reg_b(rf_1_reg_b), .RW(decoder_1_rw), .ext(\extender_1_立即数扩展 ), .PC_out(PC_EX), .RST(RST),
    .RF_we_2(WE_EX), .MemtoReg_2(MemtoReg), .jal_2(id_ex_1_jal_2), .DM_we_2(id_ex_1_dm_we_2),
    .lh_2(id_ex_1_lh_2), .bne_2(Bne), .beq_2(Beq), .bgez_2(bgez), .PC_sel_2(PC_sel), .slv_2(id_ex_1_slv_2),
    .syscall_2(id_ex_1_syscall_2), .ALU_sel_2(id_ex_1_alu_sel_2), .Y_sel_2(id_ex_1_y_sel_2),
    .X_sel_2(id_ex_1_x_sel_2), .Reg_a_2(id_ex_1_reg_a_2), .Reg_b_2(id_ex_1_reg_b_2), .RW_2(id_ex_1_rw_2),
    .ext_2(id_ex_1_ext_2), .eret(\控制器_1_eret ), .eret_2(eret), .ir_in(if_id_1_ir_out),
    .ir_out(id_ex_1_ir_out), .BUBID(hazzard_unit_1_bubid), .RA(decoder_1_r1_num), .RA_2(RA_EX),
    .RB(decoder_1_r2_num), .RB_2(RB_EX));
  ALU_IN alu_in_1 (
    .A(id_ex_1_reg_a_2), .B(id_ex_1_reg_b_2), .ext(id_ex_1_ext_2), .X(alu_in_1_x), .Y(alu_in_1_y),
    .Y_sel(id_ex_1_y_sel_2), .X_sel(id_ex_1_x_sel_2), .bgez(bgez), .slv(id_ex_1_slv_2), .sel(sel),
    .result(result), .RF_data(RF_data), .reg_a(alu_in_1_reg_a), .reg_b(alu_in_1_reg_b));
  D_Flip_Flop d_ff_1 (.clk(clk), .D(Halt), .Qn(d_ff_1_qn), .reset(RST));  // open: Q, preset, en
  Comparator #(.width(32)) comparator_1 (.a({32{1'b0}}), .b(PC_EX), .eq(comparator_1_eq));  // open: gt, lt
  Comparator #(.width(32)) comparator_2 (.a(PC_EX), .b(PC_ID), .eq(comparator_2_eq));  // open: gt, lt
  not not_2 (not_2_out, alu_1_result[0]);
  NPC npc_1 (
    .gez(not_2_out), .bgez(bgez), .beq_sign(Beq), .equal(alu_1_out_5), .bne_sign(Bne), .PC(PC_EX),
    .A(alu_in_1_reg_a), .IR(id_ex_1_ir_out), .offset(id_ex_1_ext_2), .CBScnt(CBScnt), .nPC(npc_1_npc),
    .PC_sel(PC_sel));
  ALU alu_1 (.x(alu_in_1_x), .y(alu_in_1_y), .result(alu_1_result), .out_5(alu_1_out_5), .ALU_OP(id_ex_1_alu_sel_2));
  Counter #(.width(16), .max('hffff), .trigger("falling")) counter_1 (
    .count(d_ff_1_qn), .Q(\总周期数 ), .clk(clk), .clr(RST));  // open: load, D, carry
  and and_4 (b, comparator_1_eq, comparator_2_eq);
  Syscall syscall_1 (
    .reg_b(alu_in_1_reg_b), .syscallout(SyscallOut), .halt(syscall_1_halt), .equal(alu_1_out_5),
    .syscall(id_ex_1_syscall_2), .clk(clk), .RST(RST));
  Multiplexer #(.width(32), .enable("false")) multiplexer_7 (
    .in0(multiplexer_8_out), .in1(adder_2_out), .out(RF_data), .sel(mem_wb_1_jal_2));
  EX_MEM ex_mem_1 (
    .PC_in(PC_EX), .Halt(not_1_out), .clk(clk), .RF_we(WE_EX), .MemtoReg(MemtoReg), .jal(id_ex_1_jal_2),
    .DM_we(id_ex_1_dm_we_2), .lh(id_ex_1_lh_2), .Reg_b(alu_in_1_reg_b), .Halt_2(syscall_1_halt),
    .result(alu_1_result), .RW(id_ex_1_rw_2), .PC_out(ex_mem_1_pc_out), .RST(RST),
    .RF_we_2(ex_mem_1_rf_we_2), .MemtoReg_2(ex_mem_1_memtoreg_2), .jal_2(ex_mem_1_jal_2),
    .DM_we_2(ex_mem_1_dm_we_2), .lh_2(ex_mem_1_lh_2), .Reg_b_2(ex_mem_1_reg_b_2), .Halt_3(ex_mem_1_halt_3),
    .result_2(ex_mem_1_result_2), .RW_2(ex_mem_1_rw_2));
  Multiplexer #(.width(32), .enable("false")) multiplexer_8 (
    .in0(mem_wb_1_result_2), .in1(mem_wb_1_dm_out_2), .out(multiplexer_8_out), .sel(mem_wb_1_memtoreg_2));
  MEMout memout_1 (.result(ex_mem_1_result_2), .pc(ex_mem_1_pc_out), .result_2(result), .jal(ex_mem_1_jal_2));
  Multiplexer #(.width(4), .enable("false")) multiplexer_9 (
    .in0(4'b1111), .in1(multiplexer_10_out), .out(multiplexer_9_out), .sel(ex_mem_1_lh_2));
  Multiplexer #(.width(4), .enable("false")) multiplexer_10 (
    .in0(4'b0011), .in1(4'b1100), .out(multiplexer_10_out), .sel(ex_mem_1_result_2[1]));
  // MIPS_RAM mips_ram_1: pin names not known; wires that end beside it: ex_mem_1_result_2[25:2], ex_mem_1_reg_b_2, ex_mem_1_dm_we_2, multiplexer_9_out, clk, ex_mem_1_memtoreg_2, mips_ram_1_p7
  Counter #(.width(16), .max('hffff), .trigger("falling")) counter_2 (
    .count(or_3_out), .Q(\无条件分支指令数 ), .clk(clk), .clr(RST));  // open: load, D, carry
  or or_3 (or_3_out, PC_sel[0], PC_sel[1]);
  Counter #(.width(16), .max('hffff), .trigger("falling")) counter_3 (
    .count(or_4_out), .Q(\有条件分支指令数 ), .clk(clk), .clr(RST));  // open: load, D, carry
  or or_4 (or_4_out, bgez, Beq, Bne);
  MEM_WB mem_wb_1 (
    .PC_in(ex_mem_1_pc_out), .Halt(not_1_out), .clk(clk), .RF_we(ex_mem_1_rf_we_2),
    .MemtoReg(ex_mem_1_memtoreg_2), .jal(ex_mem_1_jal_2), .Halt_2(ex_mem_1_halt_3),
    .result(ex_mem_1_result_2), .RW(ex_mem_1_rw_2), .DM_out(data_ext_1_dataout), .PC_out(mem_wb_1_pc_out),
    .RST(RST), .RF_we_2(mem_wb_1_rf_we_2), .MemtoReg_2(mem_wb_1_memtoreg_2), .jal_2(mem_wb_1_jal_2),
    .Halt_3(Halt0), .result_2(mem_wb_1_result_2), .RW_2(mem_wb_1_rw_2), .DM_out_2(mem_wb_1_dm_out_2));
  Data_ext data_ext_1 (
    .datain(mips_ram_1_p7), .dataout(data_ext_1_dataout), .bit1(ex_mem_1_result_2[1]), .lh(ex_mem_1_lh_2));
  Register #(.width(1)) register_1 (.D(Halt0), .en(not_3_out), .Q(Halt), .clk(clk), .clr(GO));
  Adder #(.width(32)) adder_2 (.a(mem_wb_1_pc_out), .b(32'h4), .out(adder_2_out));  // open: cin, cout
  not not_3 (not_3_out, Halt);
  Counter #(.width(16), .max('hffff), .trigger("falling")) counter_4 (
    .count(CBScnt), .Q(\有条件分支成功跳转 ), .clk(clk), .clr(RST));  // open: load, D, carry

  // Notes on the sheet:
  //   中断源
  //   中断等待指示
  //   数码管输出应该用寄存器锁存，否则显示数据只能一闪而过
  //   可以通过项目增加Logisim库的方式将前几次实验完成的电路作为子电路引入到本电路中使用
  //   数码管输出
  //   总复位信号应将除ROM以外所有存储组件全部清零
  //   指令存储器
  //   contents of rom_1 (hex, n*v repeats v):
  //   201d0200 20110200 20020022 112020 c 2231ffff 1620fffc 2002000a c 20150000 20160000 20170000 20080001
  //   20090003 20110876 118d00 112020 20020022 c 200b0008 1118806 1318806 112020 20020022 c 216bffff
  //   1560fff9 2002000a c 20150000 20160000 20170000 20080001 20090003 20110876 112020 20020022 c 200b0008
  //   1118804 1318804 112020 20020022 c 216bffff 1560fff9 2002000a c 20090000 200b0010 34118483 20120404
  //   118c00 129400 36318281 22520404 ad310000 2328820 21290004 216bffff 1560fffb 200b0020 20090000
  //   85310000 112020 20020022 c 21290002 216bffff 1560fff9 2002000a c 2011000f 112020 20020022 c 2231ffff
  //   621fffb 2002000a c 2002000a c afb00000 23bd0004 afb10000 23bd0004 afb20000 23bd0004 afb30000
  //   23bd0004 afb40000 23bd0004 afb50000 23bd0004 afb60000 23bd0004 afb70000 23bd0004 afa20000 23bd0004
  //   afa40000 23bd0004 20160001 20140006 20150001 168020 108100 2149825 132020 20020022 c 1600fffa
  //   295a022 1680fff7 23bdfffc 8fa40000 23bdfffc 8fa20000 23bdfffc 8fb70000 23bdfffc 8fb60000 23bdfffc
  //   8fb50000 23bdfffc 8fb40000 23bdfffc 8fb30000 23bdfffc 8fb20000 23bdfffc 8fb10000 23bdfffc 8fb00000
  //   42000018 afb00000 23bd0004 afb10000 23bd0004 afb20000 23bd0004 afb30000 23bd0004 afb40000 23bd0004
  //   afb50000 23bd0004 afb60000 23bd0004 afb70000 23bd0004 afa20000 23bd0004 afa40000 23bd0004 20160002
  //   20140006 20150001 168020 108100 2149825 132020 20020022 c 1600fffa 295a022 1680fff7 23bdfffc
  //   8fa40000 23bdfffc 8fa20000 23bdfffc 8fb70000 23bdfffc 8fb60000 23bdfffc 8fb50000 23bdfffc 8fb40000
  //   23bdfffc 8fb30000 23bdfffc 8fb20000 23bdfffc 8fb10000 23bdfffc 8fb00000 42000018 afb00000 23bd0004
  //   afb10000 23bd0004 afb20000 23bd0004 afb30000 23bd0004 afb40000 23bd0004 afb50000 23bd0004 afb60000
  //   23bd0004 afb70000 23bd0004 afa20000 23bd0004 afa40000 23bd0004 20160003 20140006 20150001 168020
  //   108100 2149825 132020 20020022 c 1600fffa 295a022 1680fff7 23bdfffc 8fa40000 23bdfffc 8fa20000
  //   23bdfffc 8fb70000 23bdfffc 8fb60000 23bdfffc 8fb50000 23bdfffc 8fb40000 23bdfffc 8fb30000 23bdfffc
  //   8fb20000 23bdfffc 8fb10000 23bdfffc 8fb00000 42000018
  //   存储单元均使用下降沿触发
  //   JR无须左移两位
  //   除了逻辑门立即数扩展为零扩展，其他均为符号扩展
  //   Continue with CCMB by one click for each instruction.
endmodule

// control
module \控制器  (
  input  [5:0] OP,
  input  [5:0] Funct,
  output [3:0] ALU_sel,
  output X_sel,
  output syscall,
  output Y_sel,
  output slv,
  output bgez,
  output shift,
  output jal,
  output imm_gates,
  output beq,
  output DM_we,
  output RF_WE,
  output rw_sel,
  output [1:0] PC_sel,
  output bne,
  output lh,
  output MemtoReg,
  output eret
);

  wire add, addi, addiu, addu, \and , andi, comparator_1_eq, comparator_16_eq, comparator_17_eq,
       comparator_18_eq, comparator_19_eq, comparator_20_eq, comparator_21_eq, comparator_22_eq,
       comparator_23_eq, comparator_24_eq, comparator_25_eq, comparator_26_eq, comparator_27_eq,
       comparator_28_eq, comparator_29_eq, comparator_30_eq, j, lw, \nor , \or , or_3_out, or_7_out,
       or_8_out, or_9_out, or_10_out, or_11_out, or_12_out, or_13_out, or_14_out, or_15_out, or_16_out,
       or_18_out, or_19_out, or_20_out, or_22_out, or_23_out, or_24_out, or_25_out, or_26_out, or_27_out,
       or_28_out, or_29_out, or_30_out, or_31_out, or_32_out, or_33_out, or_34_out, or_35_out, or_36_out,
       or_37_out, or_38_out, or_39_out, or_40_out, or_42_out, or_43_out, or_44_out, or_45_out, or_48_out,
       or_49_out, or_50_out, or_51_out, or_52_out, or_53_out, or_54_out, or_55_out, or_56_out, or_57_out,
       or_58_out, or_60_out, or_61_out, or_62_out, or_63_out, or_64_out, or_65_out, or_66_out, or_67_out,
       or_68_out, or_69_out, or_70_out, or_71_out, or_72_out, or_73_out, or_74_out, or_76_out, or_77_out,
       or_78_out, or_79_out, or_80_out, or_81_out, or_82_out, or_83_out, or_84_out, or_85_out, or_86_out,
       or_88_out, or_89_out, or_90_out, or_91_out, or_92_out, or_93_out, or_94_out, or_95_out, or_96_out,
       or_97_out, or_98_out, or_99_out, or_100_out, or_101_out, or_102_out, ori, sll, sllv, slt, slti, sltu,
       sra, srl, srlv, sub;

  Comparator #(.width(6)) comparator_1 (.a(OP), .b({6{1'b0}}), .eq(comparator_1_eq));  // open: gt, lt
  Comparator #(.width(6)) comparator_2 (.a(OP), .b(6'b001000), .eq(addi));  // open: gt, lt
  Comparator #(.width(6)) comparator_3 (.a(OP), .b(6'b001001), .eq(addiu));  // open: gt, lt
  Comparator #(.width(6)) comparator_4 (.a(OP), .b(6'b001100), .eq(andi));  // open: gt, lt
  Comparator #(.width(6)) comparator_5 (.a(OP), .b(6'b001101), .eq(ori));  // open: gt, lt
  Comparator #(.width(6)) comparator_6 (.a(OP), .b(6'b100011), .eq(lw));  // open: gt, lt
  Comparator #(.width(6)) comparator_7 (.a(OP), .b(6'b101011), .eq(DM_we));  // open: gt, lt
  Comparator #(.width(6)) comparator_8 (.a(OP), .b(6'b000100), .eq(beq));  // open: gt, lt
  Comparator #(.width(6)) comparator_9 (.a(OP), .b(6'b000101), .eq(bne));  // open: gt, lt
  Comparator #(.width(6)) comparator_10 (.a(OP), .b(6'b001010), .eq(slti));  // open: gt, lt
  Comparator #(.width(6)) comparator_11 (.a(OP), .b(6'b000010), .eq(j));  // open: gt, lt
  Comparator #(.width(6)) comparator_12 (.a(OP), .b(6'b000011), .eq(jal));  // open: gt, lt
  Comparator #(.width(6)) comparator_13 (.a(OP), .b(6'b100001), .eq(lh));  // open: gt, lt
  Comparator #(.width(6)) comparator_14 (.a(OP), .b(6'b000001), .eq(bgez));  // open: gt, lt
  Comparator #(.width(6)) comparator_15 (.a(OP), .b(6'b010000), .eq(eret));  // open: gt, lt
  Comparator #(.width(6)) comparator_16 (.a(Funct), .b(6'b100000), .eq(comparator_16_eq));  // open: gt, lt
  Comparator #(.width(6)) comparator_17 (.a(Funct), .b(6'b100001), .eq(comparator_17_eq));  // open: gt, lt
  Comparator #(.width(6)) comparator_18 (.a(Funct), .b(6'b100100), .eq(comparator_18_eq));  // open: gt, lt
  Comparator #(.width(6)) comparator_19 (.a(Funct), .b({6{1'b0}}), .eq(comparator_19_eq));  // open: gt, lt
  Comparator #(.width(6)) comparator_20 (.a(Funct), .b(6'b000011), .eq(comparator_20_eq));  // open: gt, lt
  Comparator #(.width(6)) comparator_21 (.a(Funct), .b(6'b000010), .eq(comparator_21_eq));  // open: gt, lt
  Comparator #(.width(6)) comparator_22 (.a(Funct), .b(6'b100010), .eq(comparator_22_eq));  // open: gt, lt
  Comparator #(.width(6)) comparator_23 (.a(Funct), .b(6'b100101), .eq(comparator_23_eq));  // open: gt, lt
  Comparator #(.width(6)) comparator_24 (.a(Funct), .b(6'b100111), .eq(comparator_24_eq));  // open: gt, lt
  Comparator #(.width(6)) comparator_25 (.a(Funct), .b(6'b101010), .eq(comparator_25_eq));  // open: gt, lt
  Comparator #(.width(6)) comparator_26 (.a(Funct), .b(6'b101011), .eq(comparator_26_eq));  // open: gt, lt
  Comparator #(.width(6)) comparator_27 (.a(Funct), .b(6'b001000), .eq(comparator_27_eq));  // open: gt, lt
  Comparator #(.width(6)) comparator_28 (.a(Funct), .b(6'b000110), .eq(comparator_28_eq));  // open: gt, lt
  Comparator #(.width(6)) comparator_29 (.a(Funct), .b(6'b000100), .eq(comparator_29_eq));  // open: gt, lt
  Comparator #(.width(6)) comparator_30 (.a(Funct), .b(6'b001100), .eq(comparator_30_eq));  // open: gt, lt
  and and_1 (add, comparator_1_eq, comparator_16_eq);
  and and_2 (addu, comparator_1_eq, comparator_17_eq);
  and and_3 (\and , comparator_1_eq, comparator_18_eq);
  and and_4 (sll, comparator_1_eq, comparator_19_eq);
  and and_5 (sra, comparator_1_eq, comparator_20_eq);
  and and_6 (srl, comparator_1_eq, comparator_21_eq);
  and and_7 (sub, comparator_1_eq, comparator_22_eq);
  and and_8 (\or , comparator_1_eq, comparator_23_eq);
  and and_9 (\nor , comparator_1_eq, comparator_24_eq);
  and and_10 (slt, comparator_1_eq, comparator_25_eq);
  and and_11 (sltu, comparator_1_eq, comparator_26_eq);
  and and_12 (PC_sel[1], comparator_1_eq, comparator_27_eq);
  and and_13 (srlv, comparator_1_eq, comparator_28_eq);
  and and_14 (sllv, comparator_1_eq, comparator_29_eq);
  and and_15 (syscall, comparator_1_eq, comparator_30_eq);
  or or_1 (slv, sllv, srlv);
  or or_2 (shift, sll, or_3_out);
  or or_3 (or_3_out, srl, sra);
  or or_4 (imm_gates, andi, ori);
  or or_5 (MemtoReg, lw, lh);
  or or_6 (Y_sel, addi, or_7_out);
  or or_7 (or_7_out, or_8_out, andi);
  or or_8 (or_8_out, addiu, or_9_out);
  or or_9 (or_9_out, or_10_out, sra);
  or or_10 (or_10_out, or_11_out, slti);
  or or_11 (or_11_out, srl, or_12_out);
  or or_12 (or_12_out, or_13_out, sll);
  or or_13 (or_13_out, ori, or_14_out);
  or or_14 (or_14_out, or_15_out, DM_we);
  or or_15 (or_15_out, syscall, or_16_out);
  or or_16 (or_16_out, lw, lh);
  or or_17 (X_sel, sra, or_18_out);
  or or_18 (or_18_out, srl, or_19_out);
  or or_19 (or_19_out, sll, or_20_out);
  or or_20 (or_20_out, sllv, srlv);
  or or_21 (RF_WE, addu, or_22_out);
  or or_22 (or_22_out, or_23_out, addiu);
  or or_23 (or_23_out, andi, or_24_out);
  or or_24 (or_24_out, or_25_out, addi);
  or or_25 (or_25_out, sllv, or_26_out);
  or or_26 (or_26_out, or_27_out, srlv);
  or or_27 (or_27_out, slti, or_28_out);
  or or_28 (or_28_out, or_29_out, sltu);
  or or_29 (or_29_out, add, or_30_out);
  or or_30 (or_30_out, or_31_out, sub);
  or or_31 (or_31_out, \and , or_32_out);
  or or_32 (or_32_out, or_33_out, sra);
  or or_33 (or_33_out, \nor , or_34_out);
  or or_34 (or_34_out, or_35_out, slt);
  or or_35 (or_35_out, ori, or_36_out);
  or or_36 (or_36_out, or_37_out, srl);
  or or_37 (or_37_out, sll, or_38_out);
  or or_38 (or_38_out, or_39_out, jal);
  or or_39 (or_39_out, or_40_out, lh);
  or or_40 (or_40_out, \or , lw);
  or or_41 (rw_sel, addi, or_42_out);
  or or_42 (or_42_out, or_43_out, addiu);
  or or_43 (or_43_out, or_44_out, slti);
  or or_44 (or_44_out, or_45_out, lw);
  or or_45 (or_45_out, ori, lh);
  or or_46 (PC_sel[0], j, jal);
  or or_47 (ALU_sel[3], \nor , or_48_out);
  or or_48 (or_48_out, \or , or_49_out);
  or or_49 (or_49_out, ori, or_50_out);
  or or_50 (or_50_out, or_51_out, bne);
  or or_51 (or_51_out, beq, or_52_out);
  or or_52 (or_52_out, or_53_out, sltu);
  or or_53 (or_53_out, slti, or_54_out);
  or or_54 (or_54_out, or_55_out, slt);
  or or_55 (or_55_out, jal, or_56_out);
  or or_56 (or_56_out, or_57_out, syscall);
  or or_57 (or_57_out, j, or_58_out);
  or or_58 (or_58_out, bgez, PC_sel[1]);
  or or_59 (ALU_sel[2], addi, or_60_out);
  or or_60 (or_60_out, or_61_out, addiu);
  or or_61 (or_61_out, addu, or_62_out);
  or or_62 (or_62_out, or_63_out, syscall);
  or or_63 (or_63_out, andi, or_64_out);
  or or_64 (or_64_out, or_65_out, sub);
  or or_65 (or_65_out, sltu, or_66_out);
  or or_66 (or_66_out, or_67_out, \and );
  or or_67 (or_67_out, bne, or_68_out);
  or or_68 (or_68_out, or_69_out, beq);
  or or_69 (or_69_out, add, or_70_out);
  or or_70 (or_70_out, or_71_out, jal);
  or or_71 (or_71_out, PC_sel[1], or_72_out);
  or or_72 (or_72_out, or_73_out, DM_we);
  or or_73 (or_73_out, lw, or_74_out);
  or or_74 (or_74_out, j, lh);
  or or_75 (ALU_sel[1], \and , or_76_out);
  or or_76 (or_76_out, or_77_out, andi);
  or or_77 (or_77_out, srl, or_78_out);
  or or_78 (or_78_out, or_79_out, sub);
  or or_79 (or_79_out, \nor , or_80_out);
  or or_80 (or_80_out, or_81_out, slti);
  or or_81 (or_81_out, srlv, or_82_out);
  or or_82 (or_82_out, or_83_out, slt);
  or or_83 (or_83_out, jal, or_84_out);
  or or_84 (or_84_out, or_85_out, syscall);
  or or_85 (or_85_out, PC_sel[1], or_86_out);
  or or_86 (or_86_out, j, bgez);
  or or_87 (ALU_sel[0], addu, or_88_out);
  or or_88 (or_88_out, or_89_out, addiu);
  or or_89 (or_89_out, andi, or_90_out);
  or or_90 (or_90_out, or_91_out, add);
  or or_91 (or_91_out, addi, or_92_out);
  or or_92 (or_92_out, or_93_out, \and );
  or or_93 (or_93_out, sra, or_94_out);
  or or_94 (or_94_out, or_95_out, slti);
  or or_95 (or_95_out, slt, or_96_out);
  or or_96 (or_96_out, or_97_out, syscall);
  or or_97 (or_97_out, or_98_out, jal);
  or or_98 (or_98_out, lh, or_99_out);
  or or_99 (or_99_out, j, or_100_out);
  or or_100 (or_100_out, or_101_out, DM_we);
  or or_101 (or_101_out, PC_sel[1], or_102_out);
  or or_102 (or_102_out, bgez, lw);

  // Other names for the same wires on the sheet: jr = PC_sel[1]; sw = DM_we
endmodule

// Ext
module Extender (
  input  syscall,
  input  [15:0] \立即数 ,
  input  imm_gates,
  input  shift,
  output [31:0] \立即数扩展 ,
  output [31:0] offset
);

  wire [15:0] multiplexer_1_out;
  wire [31:0] bit_extender_1_out, bit_extender_2_out, bit_extender_3_out, multiplexer_2_out;

  Multiplexer #(.width(16), .enable("false")) multiplexer_1 (
    .in0(\立即数 ), .in1(16'ha), .out(multiplexer_1_out), .sel(syscall));
  assign bit_extender_1_out = {{16{multiplexer_1_out[15]}}, multiplexer_1_out};  // Bit_Extender bit_extender_1
  assign bit_extender_2_out = {{16{1'b0}}, multiplexer_1_out};  // Bit_Extender bit_extender_2
  assign bit_extender_3_out = {{27{\立即数 [10]}}, \立即数 [10:6]};  // Bit_Extender bit_extender_3
  assign offset = {{16{\立即数 [15]}}, \立即数 };  // Bit_Extender bit_extender_4
  Multiplexer #(.width(32), .enable("false")) multiplexer_2 (
    .in0(bit_extender_1_out), .in1(bit_extender_2_out), .out(multiplexer_2_out), .sel(imm_gates));
  Multiplexer #(.width(32), .enable("false")) multiplexer_3 (
    .in0(multiplexer_2_out), .in1(bit_extender_3_out), .out(\立即数扩展 ), .sel(shift));
endmodule

module Decoder (
  input  syscall,
  input  [31:0] PC,
  input  rW_sel,
  input  jal,
  output [5:0] OP,
  output [5:0] FUNC,
  output [4:0] R1_num,
  output [4:0] R2_num,
  output [4:0] RW,
  output [15:0] \立即数 
);

  wire [4:0] multiplexer_3_out;

  Multiplexer #(.width(5), .enable("false")) multiplexer_1 (
    .in0(PC[25:21]), .in1(5'b00010), .out(R1_num), .sel(syscall));
  Multiplexer #(.width(5), .enable("false")) multiplexer_2 (
    .in0(PC[20:16]), .in1(5'b00100), .out(R2_num), .sel(syscall));
  Multiplexer #(.width(5), .enable("false")) multiplexer_3 (
    .in0(PC[15:11]), .in1(PC[20:16]), .out(multiplexer_3_out), .sel(rW_sel));
  Multiplexer #(.width(5), .enable("false")) multiplexer_4 (
    .in0(multiplexer_3_out), .in1({5{1'b1}}), .out(RW), .sel(jal));

  assign FUNC = PC[5:0];
  assign OP = PC[31:26];
  assign \立即数  = PC[15:0];
endmodule

module NPC (
  input  gez,
  input  bgez,
  input  beq_sign,
  input  equal,
  input  bne_sign,
  input  [1:0] PC_sel,
  input  [31:0] PC,
  input  [31:0] A,
  input  [31:0] IR,
  input  [31:0] offset,
  output CBScnt,
  output [31:0] nPC
);

  wire and_1_out, and_2_out, and_3_out, not_1_out;
  wire [31:0] adder_1_out, adder_2_out, multiplexer_1_out, shifter_1_out;

  Adder #(.width(32)) adder_1 (.a(PC), .b(32'h4), .out(adder_1_out));  // open: cin, cout
  Shifter #(.width(32)) shifter_1 (.in(offset), .\dist (5'b00010), .out(shifter_1_out));
  not not_1 (not_1_out, equal);
  Adder #(.width(32)) adder_2 (.a(adder_1_out), .b(shifter_1_out), .out(adder_2_out));  // open: cin, cout
  and and_1 (and_1_out, gez, bgez);
  and and_2 (and_2_out, beq_sign, equal);
  and and_3 (and_3_out, not_1_out, bne_sign);
  or or_1 (CBScnt, and_1_out, and_2_out, and_3_out);
  Multiplexer #(.select(2), .width(32), .enable("false")) multiplexer_1 (
    .in0(adder_1_out), .in1({4'b0000, IR[25:0], 2'b00}), .in2(A), .in3({32{1'b0}}), .out(multiplexer_1_out),
    .sel(PC_sel));
  Multiplexer #(.width(32), .enable("false")) multiplexer_2 (
    .in0(multiplexer_1_out), .in1(adder_2_out), .out(nPC), .sel(CBScnt));
endmodule

module ALU (
  input  [31:0] x,
  input  [31:0] y,
  input  [3:0] ALU_OP,
  output [31:0] result,
  output out_5
);

  ALU_part alu_1 (
    .AluOP(ALU_OP), .X(x), .Equal(out_5), .Result(result), .Y(y));  // open: Signed_Overflow, Result_2, UnSigned_Overflow
endmodule

module RF (
  input  [31:0] data,
  input  clk,
  input  we,
  input  [4:0] rw,
  input  [4:0] rb,
  input  [4:0] ra,
  output [31:0] reg_a,
  output [31:0] reg_b
);

  // RegisterFile registerfile_1: pin names not known; wires that end beside it: data, clk, we, rw, ra, rb, reg_a, reg_b
endmodule

module IF_ID (
  input  Halt,
  input  [31:0] PC_in,
  input  [31:0] ir_in,
  input  BUBIF,
  input  clk,
  input  clear,
  output [31:0] PC_out,
  output [31:0] ir_out
);

  wire [31:0] multiplexer_1_out, multiplexer_2_out;

  Multiplexer #(.width(32), .enable("false")) multiplexer_1 (
    .in0(PC_in), .in1({32{1'b0}}), .out(multiplexer_1_out), .sel(BUBIF));
  Multiplexer #(.width(32), .enable("false")) multiplexer_2 (
    .in0(ir_in), .in1({32{1'b0}}), .out(multiplexer_2_out), .sel(BUBIF));
  Register #(.width(32)) register_1 (.D(multiplexer_1_out), .en(Halt), .Q(PC_out), .clk(clk), .clr(clear));
  Register #(.width(32)) register_2 (.D(multiplexer_2_out), .en(Halt), .Q(ir_out), .clk(clk), .clr(clear));
endmodule

// ALU_in
module ALU_IN (
  input  [31:0] A,
  input  bgez,
  input  Y_sel,
  input  X_sel,
  input  slv,
  input  [31:0] RF_data,
  input  [31:0] B,
  input  [31:0] result,
  input  [31:0] ext,
  input  [3:0] sel,
  output [31:0] reg_a,
  output [31:0] X,
  output [31:0] Y,
  output [31:0] reg_b
);

  wire [31:0] multiplexer_1_out, multiplexer_2_out, multiplexer_5_out, multiplexer_7_out;

  Multiplexer #(.width(32), .enable("false")) multiplexer_1 (
    .in0(A), .in1(RF_data), .out(multiplexer_1_out), .sel(sel[0]));
  Multiplexer #(.width(32), .enable("false")) multiplexer_2 (
    .in0(B), .in1(RF_data), .out(multiplexer_2_out), .sel(sel[1]));
  Multiplexer #(.width(32), .enable("false")) multiplexer_3 (
    .in0(multiplexer_1_out), .in1(result), .out(reg_a), .sel(sel[2]));
  Multiplexer #(.width(32), .enable("false")) multiplexer_4 (
    .in0(multiplexer_2_out), .in1(result), .out(reg_b), .sel(sel[3]));
  Multiplexer #(.width(32), .enable("false")) multiplexer_5 (
    .in0(reg_b), .in1(ext), .out(multiplexer_5_out), .sel(Y_sel));
  Multiplexer #(.width(32), .enable("false")) multiplexer_6 (.in0(reg_a), .in1(reg_b), .out(X), .sel(X_sel));
  Multiplexer #(.width(32), .enable("false")) multiplexer_7 (
    .in0(multiplexer_5_out), .in1({32{1'b0}}), .out(multiplexer_7_out), .sel(bgez));
  Multiplexer #(.width(32), .enable("false")) multiplexer_8 (.in0(multiplexer_7_out), .in1(reg_a), .out(Y), .sel(slv));
endmodule

module ID_EX (
  input  [31:0] PC_in,
  input  Halt,
  input  clk,
  input  [31:0] ir_in,
  input  [4:0] RA,
  input  [4:0] RB,
  input  RST,
  input  RF_we,
  input  MemtoReg,
  input  jal,
  input  DM_we,
  input  lh,
  input  bne,
  input  beq,
  input  bgez,
  input  [1:0] PC_sel,
  input  slv,
  input  syscall,
  input  [3:0] ALU_sel,
  input  Y_sel,
  input  X_sel,
  input  [31:0] Reg_a,
  input  [31:0] Reg_b,
  input  [4:0] RW,
  input  [31:0] ext,
  input  eret,
  input  BUBID,
  output [31:0] PC_out,
  output [31:0] ir_out,
  output [4:0] RA_2,
  output [4:0] RB_2,
  output RF_we_2,
  output MemtoReg_2,
  output jal_2,
  output DM_we_2,
  output lh_2,
  output bne_2,
  output beq_2,
  output bgez_2,
  output [1:0] PC_sel_2,
  output slv_2,
  output syscall_2,
  output [3:0] ALU_sel_2,
  output Y_sel_2,
  output X_sel_2,
  output [31:0] Reg_a_2,
  output [31:0] Reg_b_2,
  output [4:0] RW_2,
  output [31:0] ext_2,
  output eret_2
);

  wire multiplexer_5_out, multiplexer_6_out, multiplexer_7_out, multiplexer_8_out, multiplexer_9_out,
       multiplexer_10_out, multiplexer_11_out, multiplexer_12_out, multiplexer_14_out, multiplexer_15_out,
       multiplexer_17_out, multiplexer_18_out, multiplexer_23_out;
  wire [1:0] multiplexer_13_out;
  wire [3:0] multiplexer_16_out;
  wire [4:0] multiplexer_3_out, multiplexer_4_out, multiplexer_21_out;
  wire [31:0] multiplexer_1_out, multiplexer_2_out, multiplexer_19_out, multiplexer_20_out,
       multiplexer_22_out;

  Multiplexer #(.width(32), .enable("false")) multiplexer_1 (
    .in0(PC_in), .in1({32{1'b0}}), .out(multiplexer_1_out), .sel(BUBID));
  Multiplexer #(.width(32), .enable("false")) multiplexer_2 (
    .in0(ir_in), .in1({32{1'b0}}), .out(multiplexer_2_out), .sel(BUBID));
  Multiplexer #(.width(5), .enable("false")) multiplexer_3 (
    .in0(RA), .in1({5{1'b0}}), .out(multiplexer_3_out), .sel(BUBID));
  Multiplexer #(.width(5), .enable("false")) multiplexer_4 (
    .in0(RB), .in1({5{1'b0}}), .out(multiplexer_4_out), .sel(BUBID));
  Multiplexer #(.enable("false")) multiplexer_5 (.in0(RF_we), .in1(1'b0), .out(multiplexer_5_out), .sel(BUBID));
  Multiplexer #(.enable("false")) multiplexer_6 (.in0(MemtoReg), .in1(1'b0), .out(multiplexer_6_out), .sel(BUBID));
  Multiplexer #(.enable("false")) multiplexer_7 (.in0(jal), .in1(1'b0), .out(multiplexer_7_out), .sel(BUBID));
  Multiplexer #(.enable("false")) multiplexer_8 (.in0(DM_we), .in1(1'b0), .out(multiplexer_8_out), .sel(BUBID));
  Multiplexer #(.enable("false")) multiplexer_9 (.in0(lh), .in1(1'b0), .out(multiplexer_9_out), .sel(BUBID));
  Multiplexer #(.enable("false")) multiplexer_10 (.in0(bne), .in1(1'b0), .out(multiplexer_10_out), .sel(BUBID));
  Multiplexer #(.enable("false")) multiplexer_11 (.in0(beq), .in1(1'b0), .out(multiplexer_11_out), .sel(BUBID));
  Multiplexer #(.enable("false")) multiplexer_12 (.in0(bgez), .in1(1'b0), .out(multiplexer_12_out), .sel(BUBID));
  Multiplexer #(.width(2), .enable("false")) multiplexer_13 (
    .in0(PC_sel), .in1(2'b00), .out(multiplexer_13_out), .sel(BUBID));
  Multiplexer #(.enable("false")) multiplexer_14 (.in0(slv), .in1(1'b0), .out(multiplexer_14_out), .sel(BUBID));
  Multiplexer #(.enable("false")) multiplexer_15 (.in0(syscall), .in1(1'b0), .out(multiplexer_15_out), .sel(BUBID));
  Multiplexer #(.width(4), .enable("false")) multiplexer_16 (
    .in0(ALU_sel), .in1(4'b0000), .out(multiplexer_16_out), .sel(BUBID));
  Multiplexer #(.enable("false")) multiplexer_17 (.in0(Y_sel), .in1(1'b0), .out(multiplexer_17_out), .sel(BUBID));
  Multiplexer #(.enable("false")) multiplexer_18 (.in0(X_sel), .in1(1'b0), .out(multiplexer_18_out), .sel(BUBID));
  Multiplexer #(.width(32), .enable("false")) multiplexer_19 (
    .in0(Reg_a), .in1({32{1'b0}}), .out(multiplexer_19_out), .sel(BUBID));
  Multiplexer #(.width(32), .enable("false")) multiplexer_20 (
    .in0(Reg_b), .in1({32{1'b0}}), .out(multiplexer_20_out), .sel(BUBID));
  Multiplexer #(.width(5), .enable("false")) multiplexer_21 (
    .in0(RW), .in1({5{1'b0}}), .out(multiplexer_21_out), .sel(BUBID));
  Multiplexer #(.width(32), .enable("false")) multiplexer_22 (
    .in0(ext), .in1({32{1'b0}}), .out(multiplexer_22_out), .sel(BUBID));
  Multiplexer #(.enable("false")) multiplexer_23 (.in0(eret), .in1(1'b0), .out(multiplexer_23_out), .sel(BUBID));
  Register #(.width(32)) register_1 (.D(multiplexer_1_out), .en(Halt), .Q(PC_out), .clk(clk), .clr(RST));
  Register #(.width(32)) register_2 (.D(multiplexer_2_out), .en(Halt), .Q(ir_out), .clk(clk), .clr(RST));
  Register #(.width(5)) register_3 (.D(multiplexer_3_out), .en(Halt), .Q(RA_2), .clk(clk), .clr(RST));
  Register #(.width(5)) register_4 (.D(multiplexer_4_out), .en(Halt), .Q(RB_2), .clk(clk), .clr(RST));
  Register #(.width(1)) register_5 (.D(multiplexer_5_out), .en(Halt), .Q(RF_we_2), .clk(clk), .clr(RST));
  Register #(.width(1)) register_6 (.D(multiplexer_6_out), .en(Halt), .Q(MemtoReg_2), .clk(clk), .clr(RST));
  Register #(.width(1)) register_7 (.D(multiplexer_7_out), .en(Halt), .Q(jal_2), .clk(clk), .clr(RST));
  Register #(.width(1)) register_8 (.D(multiplexer_8_out), .en(Halt), .Q(DM_we_2), .clk(clk), .clr(RST));
  Register #(.width(1)) register_9 (.D(multiplexer_9_out), .en(Halt), .Q(lh_2), .clk(clk), .clr(RST));
  Register #(.width(1)) register_10 (.D(multiplexer_10_out), .en(Halt), .Q(bne_2), .clk(clk), .clr(RST));
  Register #(.width(1)) register_11 (.D(multiplexer_11_out), .en(Halt), .Q(beq_2), .clk(clk), .clr(RST));
  Register #(.width(1)) register_12 (.D(multiplexer_12_out), .en(Halt), .Q(bgez_2), .clk(clk), .clr(RST));
  Register #(.width(2)) register_13 (.D(multiplexer_13_out), .en(Halt), .Q(PC_sel_2), .clk(clk), .clr(RST));
  Register #(.width(1)) register_14 (.D(multiplexer_14_out), .en(Halt), .Q(slv_2), .clk(clk), .clr(RST));
  Register #(.width(1)) register_15 (.D(multiplexer_15_out), .en(Halt), .Q(syscall_2), .clk(clk), .clr(RST));
  Register #(.width(4)) register_16 (.D(multiplexer_16_out), .en(Halt), .Q(ALU_sel_2), .clk(clk), .clr(RST));
  Register #(.width(1)) register_17 (.D(multiplexer_17_out), .en(Halt), .Q(Y_sel_2), .clk(clk), .clr(RST));
  Register #(.width(1)) register_18 (.D(multiplexer_18_out), .en(Halt), .Q(X_sel_2), .clk(clk), .clr(RST));
  Register #(.width(32)) register_19 (.D(multiplexer_19_out), .en(Halt), .Q(Reg_a_2), .clk(clk), .clr(RST));
  Register #(.width(32)) register_20 (.D(multiplexer_20_out), .en(Halt), .Q(Reg_b_2), .clk(clk), .clr(RST));
  Register #(.width(5)) register_21 (.D(multiplexer_21_out), .en(Halt), .Q(RW_2), .clk(clk), .clr(RST));
  Register #(.width(32)) register_22 (.D(multiplexer_22_out), .en(Halt), .Q(ext_2), .clk(clk), .clr(RST));
  Register #(.width(1)) register_23 (.D(multiplexer_23_out), .en(Halt), .Q(eret_2), .clk(clk), .clr(RST));
endmodule

// syscall
module Syscall (
  input  equal,
  input  syscall,
  input  [31:0] reg_b,
  input  clk,
  input  RST,
  output [31:0] syscallout,
  output halt
);

  wire and_2_out, not_1_out;

  not not_1 (not_1_out, equal);
  and and_1 (halt, equal, syscall);
  and and_2 (and_2_out, syscall, not_1_out);
  Register #(.width(32)) register_1 (.D(reg_b), .en(and_2_out), .Q(syscallout), .clk(clk), .clr(RST));
endmodule

module EX_MEM (
  input  [31:0] PC_in,
  input  Halt,
  input  clk,
  input  RST,
  input  RF_we,
  input  MemtoReg,
  input  jal,
  input  DM_we,
  input  lh,
  input  [31:0] Reg_b,
  input  Halt_2,
  input  [31:0] result,
  input  [4:0] RW,
  output [31:0] PC_out,
  output RF_we_2,
  output MemtoReg_2,
  output jal_2,
  output DM_we_2,
  output lh_2,
  output [31:0] Reg_b_2,
  output Halt_3,
  output [31:0] result_2,
  output [4:0] RW_2
);

  Register #(.width(32)) register_1 (.D(PC_in), .en(Halt), .Q(PC_out), .clk(clk), .clr(RST));
  Register #(.width(1)) register_2 (.D(RF_we), .en(Halt), .Q(RF_we_2), .clk(clk), .clr(RST));
  Register #(.width(1)) register_3 (.D(MemtoReg), .en(Halt), .Q(MemtoReg_2), .clk(clk), .clr(RST));
  Register #(.width(1)) register_4 (.D(jal), .en(Halt), .Q(jal_2), .clk(clk), .clr(RST));
  Register #(.width(1)) register_5 (.D(DM_we), .en(Halt), .Q(DM_we_2), .clk(clk), .clr(RST));
  Register #(.width(1)) register_6 (.D(lh), .en(Halt), .Q(lh_2), .clk(clk), .clr(RST));
  Register #(.width(32)) register_7 (.D(Reg_b), .en(Halt), .Q(Reg_b_2), .clk(clk), .clr(RST));
  Register #(.width(1)) register_8 (.D(Halt_2), .en(Halt), .Q(Halt_3), .clk(clk), .clr(RST));
  Register #(.width(32)) register_9 (.D(result), .en(Halt), .Q(result_2), .clk(clk), .clr(RST));
  Register #(.width(5)) register_10 (.D(RW), .en(Halt), .Q(RW_2), .clk(clk), .clr(RST));
endmodule

module MEM_WB (
  input  [31:0] PC_in,
  input  Halt,
  input  clk,
  input  RST,
  input  RF_we,
  input  MemtoReg,
  input  jal,
  input  Halt_2,
  input  [31:0] result,
  input  [4:0] RW,
  input  [31:0] DM_out,
  output [31:0] PC_out,
  output RF_we_2,
  output MemtoReg_2,
  output jal_2,
  output Halt_3,
  output [31:0] result_2,
  output [4:0] RW_2,
  output [31:0] DM_out_2
);

  Register #(.width(32)) register_1 (.D(PC_in), .en(Halt), .Q(PC_out), .clk(clk), .clr(RST));
  Register #(.width(1)) register_2 (.D(RF_we), .en(Halt), .Q(RF_we_2), .clk(clk), .clr(RST));
  Register #(.width(1)) register_3 (.D(MemtoReg), .en(Halt), .Q(MemtoReg_2), .clk(clk), .clr(RST));
  Register #(.width(1)) register_4 (.D(jal), .en(Halt), .Q(jal_2), .clk(clk), .clr(RST));
  Register #(.width(1)) register_5 (.D(Halt_2), .en(Halt), .Q(Halt_3), .clk(clk), .clr(RST));
  Register #(.width(32)) register_6 (.D(result), .en(Halt), .Q(result_2), .clk(clk), .clr(RST));
  Register #(.width(5)) register_7 (.D(RW), .en(Halt), .Q(RW_2), .clk(clk), .clr(RST));
  Register #(.width(32)) register_8 (.D(DM_out), .en(Halt), .Q(DM_out_2), .clk(clk), .clr(RST));
endmodule

module Hazzard_Unit (
  input  [4:0] RAID,
  input  WE_EX,
  input  MemtoReg,
  input  nHalt,
  input  [4:0] RWEX,
  input  [4:0] RBID,
  input  Jump,
  input  irie,
  input  eret,
  input  [4:0] RAEX,
  input  [4:0] RWWB,
  input  [4:0] RBEX,
  input  WE_WB,
  input  [4:0] RWMEM,
  input  WE_MEM,
  input  clk,
  input  rst,
  output [15:0] \气泡数 ,
  output Stall,
  output BUBID,
  output BUBIF,
  output [3:0] sel
);

  wire and_1_out, and_2_out, and_3_out, and_4_out, and_5_out, and_10_out, and_11_out, and_12_out,
       comparator_1_eq, comparator_2_eq, comparator_3_eq, comparator_4_eq, comparator_5_eq, comparator_6_eq,
       comparator_7_eq, comparator_8_eq, comparator_9_eq, comparator_10_eq, comparator_11_eq, not_1_out,
       not_2_out, not_3_out, not_4_out, not_5_out, not_6_out, not_7_out, or_1_out, or_2_out;

  Comparator #(.width(5)) comparator_1 (.a({5{1'b0}}), .b(RWEX), .eq(comparator_1_eq));  // open: gt, lt
  Comparator #(.width(5)) comparator_2 (.a(RAID), .b(RWEX), .eq(comparator_2_eq));  // open: gt, lt
  Comparator #(.width(5)) comparator_3 (.a(RWEX), .b(RBID), .eq(comparator_3_eq));  // open: gt, lt
  Comparator #(.width(5)) comparator_4 (.a({5{1'b0}}), .b(RWWB), .eq(comparator_4_eq));  // open: gt, lt
  not not_1 (not_1_out, comparator_4_eq);
  Comparator #(.width(5)) comparator_5 (.a(RAEX), .b(RWWB), .eq(comparator_5_eq));  // open: gt, lt
  Comparator #(.width(5)) comparator_6 (.a(RWWB), .b(RBEX), .eq(comparator_6_eq));  // open: gt, lt
  not not_2 (not_2_out, comparator_7_eq);
  Comparator #(.width(5)) comparator_7 (.a(RWWB), .b({5{1'b0}}), .eq(comparator_7_eq));  // open: gt, lt
  Comparator #(.width(5)) comparator_8 (.a({5{1'b0}}), .b(RWMEM), .eq(comparator_8_eq));  // open: gt, lt
  Comparator #(.width(5)) comparator_9 (.a(RAEX), .b(RWMEM), .eq(comparator_9_eq));  // open: gt, lt
  Comparator #(.width(5)) comparator_10 (.a(RWMEM), .b(RBEX), .eq(comparator_10_eq));  // open: gt, lt
  Comparator #(.width(5)) comparator_11 (.a(RWMEM), .b({5{1'b0}}), .eq(comparator_11_eq));  // open: gt, lt
  not not_3 (not_3_out, comparator_1_eq);
  and and_1 (and_1_out, not_1_out, comparator_5_eq);
  and and_2 (and_2_out, comparator_6_eq, not_2_out);
  not not_4 (not_4_out, comparator_8_eq);
  not not_5 (not_5_out, comparator_11_eq);
  and and_3 (and_3_out, not_3_out, or_1_out);
  or or_1 (or_1_out, comparator_2_eq, comparator_3_eq);
  or or_2 (or_2_out, irie, eret);
  and and_4 (and_4_out, not_4_out, comparator_9_eq);
  and and_5 (and_5_out, comparator_10_eq, not_5_out);
  and and_6 (sel[0], WE_WB, and_1_out);
  and and_7 (sel[1], WE_WB, and_2_out);
  and and_8 (sel[2], WE_MEM, and_4_out);
  and and_9 (sel[3], WE_MEM, and_5_out);
  and and_10 (and_10_out, WE_EX, MemtoReg, and_3_out);
  not not_6 (not_6_out, Jump);
  and and_11 (and_11_out, and_10_out, not_6_out);
  not not_7 (not_7_out, and_11_out);
  and and_12 (and_12_out, and_11_out, nHalt);
  and and_13 (Stall, nHalt, not_7_out);
  or or_3 (BUBID, and_11_out, or_2_out, Jump);
  or or_4 (BUBIF, Jump, or_2_out);
  Counter #(.width(16), .max('hffff)) counter_1 (
    .count(and_12_out), .Q(\气泡数 ), .clk(clk), .clr(rst));  // open: load, D, carry
endmodule

module Data_ext (
  input  [31:0] datain,
  input  lh,
  input  bit1,
  output [31:0] dataout
);

  wire [31:0] bit_extender_1_out, bit_extender_2_out, multiplexer_1_out;

  assign bit_extender_1_out = {{16{datain[15]}}, datain[15:0]};  // Bit_Extender bit_extender_1
  assign bit_extender_2_out = {{16{datain[31]}}, datain[31:16]};  // Bit_Extender bit_extender_2
  Multiplexer #(.width(32), .enable("false")) multiplexer_1 (
    .in0(bit_extender_1_out), .in1(bit_extender_2_out), .out(multiplexer_1_out), .sel(bit1));
  Multiplexer #(.width(32), .enable("false")) multiplexer_2 (
    .in0(datain), .in1(multiplexer_1_out), .out(dataout), .sel(lh));
endmodule

module MEMout (
  input  [31:0] result,
  input  [31:0] pc,
  input  jal,
  output [31:0] result_2
);

  wire [31:0] adder_1_out;

  Adder #(.width(32)) adder_1 (.a(pc), .b(32'h4), .out(adder_1_out));  // open: cin, cout
  Multiplexer #(.width(32), .enable("false")) multiplexer_1 (
    .in0(result), .in1(adder_1_out), .out(result_2), .sel(jal));
endmodule

module interrupt (
  input  \_1号中断 ,
  input  \_2号中断 ,
  input  \_3号中断 ,
  input  clk,
  input  eret,
  output \_1号中断等待指示 ,
  output \_2号中断等待指示 ,
  output \_3号中断等待指示 ,
  output [1:0] XY,
  output IR,
  output IE
);

  wire \_1号清零 , \_2号清零 , \_3号清零 , and_1_out, and_2_out, and_3_out, and_4_out, and_5_out, d_ff_1_q, d_ff_2_q,
       d_ff_3_q, d_ff_4_q, IR1_2_q, IR1_3_q, IR1_q, or_4_out, or_5_out, or_6_out, or_7_out;
  wire [1:0] multiplexer_1_out, multiplexer_2_out, register_1_q;

  or or_1 (\_1号中断等待指示 , IR1_q, d_ff_1_q);
  or or_2 (\_2号中断等待指示 , IR1_2_q, d_ff_2_q);
  or or_3 (\_3号中断等待指示 , IR1_3_q, d_ff_3_q);
  D_Flip_Flop d_ff_1 (.clk(\_1号中断 ), .D(1'b1), .Q(d_ff_1_q), .reset(IR1_q));  // open: Qn, preset, en
  D_Flip_Flop d_ff_2 (.clk(\_2号中断 ), .D(1'b1), .Q(d_ff_2_q), .reset(IR1_2_q));  // open: Qn, preset, en
  D_Flip_Flop d_ff_3 (.clk(\_3号中断 ), .D(1'b1), .Q(d_ff_3_q), .reset(IR1_3_q));  // open: Qn, preset, en
  or or_4 (or_4_out, IR, d_ff_4_q);
  or or_5 (or_5_out, d_ff_1_q, IR1_q);
  or or_6 (or_6_out, d_ff_2_q, IR1_2_q);
  or or_7 (or_7_out, d_ff_3_q, IR1_3_q);
  and and_1 (and_1_out, or_5_out, ~\_1号清零 );  // AND_Gate
  and and_2 (and_2_out, or_6_out, ~\_2号清零 );  // AND_Gate
  and and_3 (and_3_out, or_7_out, ~\_3号清零 );  // AND_Gate
  and and_4 (and_4_out, or_4_out, ~eret);  // AND_Gate
  D_Flip_Flop IR1 (.clk(clk), .D(and_1_out), .Q(IR1_q));  // open: Qn, preset, en, reset
  D_Flip_Flop IR1_2 (.clk(clk), .D(and_2_out), .Q(IR1_2_q));  // open: Qn, preset, en, reset
  D_Flip_Flop IR1_3 (.clk(clk), .D(and_3_out), .Q(IR1_3_q));  // open: Qn, preset, en, reset
  D_Flip_Flop d_ff_4 (.clk(clk), .D(and_4_out), .Q(d_ff_4_q));  // open: Qn, preset, en, reset
  not not_1 (IE, d_ff_4_q);
  or or_8 (IR, \_1号中断等待指示 , \_2号中断等待指示 , \_3号中断等待指示 );
  and and_5 (and_5_out, IR, IE);
  Multiplexer #(.width(2), .enable("false")) multiplexer_1 (
    .in0(2'b00), .in1(2'b01), .out(multiplexer_1_out), .sel(\_1号中断等待指示 ));
  Multiplexer #(.width(2), .enable("false")) multiplexer_2 (
    .in0(multiplexer_1_out), .in1(2'b10), .out(multiplexer_2_out), .sel(\_2号中断等待指示 ));
  Multiplexer #(.width(2), .enable("false")) multiplexer_3 (
    .in0(multiplexer_2_out), .in1(2'b11), .out(XY), .sel(\_3号中断等待指示 ));
  Register #(.width(2)) register_1 (.D(XY), .en(and_5_out), .Q(register_1_q), .clk(clk));  // open: clr
  Demultiplexer #(.select(2), .enable("false")) demultiplexer_1 (
    .out1(\_1号清零 ), .out2(\_2号清零 ), .out3(\_3号清零 ), .in(eret), .sel(register_1_q));  // open: out0

  // Other names for the same wires on the sheet: X = XY[0]; Y = XY[1]

  // Notes on the sheet:
  //   中断信号源及指示电路规范（优先级3>2>1>CPU(0）)
  //   Reset 
  //   Reset 
  //   Reset 
endmodule
